// Logisim project RISC_V_32.circ as structural Verilog: 12 circuits, main circuit Microcontroller
module CPU (
  input  [31:0] juhis,
  input  [31:0] malu_sisend,
  input  reset,
  input  clk,
  input  [19:0] Ext_Interrupt,
  output [31:0] juhise_aadress,
  output [31:0] ALU_valjund,
  output kirjuta_mallu,
  output [31:0] malu_valjund
);

  wire and_1_out, and_2_out, and_3_out, and_4_out, and_5_out, and_6_out, and_7_out, and_8_out, and_9_out,
       and_10_out, and_11_out, and_12_out, and_13_out, and_14_out, and_15_out, and_16_out, and_17_out,
       and_18_out, and_19_out, and_20_out, and_21_out, and_22_out, and_23_out, and_24_out, and_25_out,
       and_26_out, and_27_out, and_28_out, and_29_out, and_30_out, and_31_out, and_32_out, and_33_out,
       and_34_out, comparator_1_eq, comparator_2_eq, comparator_3_eq, comparator_4_eq, comparator_5_eq,
       comparator_6_eq, comparator_7_eq, comparator_8_eq, Instruction_decoder_1_alu_src_a,
       Instruction_decoder_1_alu_src_b, Instruction_decoder_1_branch_select,
       Instruction_decoder_1_kehtiv_opcode, Katkestus, kirjutaCSR, MIE, mret, multiplexer_4_out, not_1_out,
       not_2_out, or_1_out, or_2_out, or_4_out, or_5_out, or_6_out, or_7_out, or_8_out, or_9_out, or_10_out,
       or_11_out, or_12_out, or_13_out, or_14_out, or_15_out, or_16_out, or_17_out, or_18_out, or_19_out,
       or_20_out, or_21_out, or_22_out, or_23_out, or_24_out, or_25_out, or_26_out, or_27_out, or_28_out,
       or_29_out, or_30_out, or_31_out, or_32_out, or_33_out, or_34_out, or_36_out, or_37_out, or_38_out,
       or_39_out, or_40_out, or_41_out, or_42_out, or_43_out, or_44_out, or_45_out, or_46_out, or_47_out,
       or_48_out, or_49_out, or_50_out, or_51_out, or_52_out, or_53_out, or_54_out, or_55_out, or_56_out,
       or_57_out, or_58_out, or_59_out, or_60_out, or_61_out, or_62_out, or_63_out, or_64_out, or_65_out,
       or_67_out, or_68_out, s_r_ff_1_q, s_r_ff_2_q, s_r_ff_3_q, tundmatu_opcode, undriven, undriven_2,
       undriven_3, VJKA;
  wire [1:0] Instruction_decoder_1_register_mux;
  wire [2:0] Instruction_decoder_1_data_type, Instruction_decoder_1_pc_controll;
  wire [3:0] multiplexer_8_out, shifter_1_out;
  wire [4:0] Instruction_decoder_1_command, Instruction_decoder_1_rd, Instruction_decoder_1_rs1,
       Instruction_decoder_1_rs2;
  wire [11:0] CSRaadress;
  wire [17:17] register_2_q_2;
  wire [29:0] register_1_q, register_2_q;
  wire [31:0] adder_1_out, and_35_out, bit_extender_1_out, bit_extender_2_out, bit_extender_3_out,
       bit_extender_4_out, controlled_buffer_1_out, controlled_buffer_32_out, counter_1_q, CSRvaljund,
       Instruction_decoder_1_immidiate, KatkestuseAadress, multiplexer_2_out, multiplexer_3_out,
       multiplexer_5_out, multiplexer_6_out, multiplexer_7_out, multiplexer_9_out, multiplexer_10_out,
       multiplexer_11_out, multiplexer_12_out, not_4_out, or_69_out, Registers_1_register_output_1,
       Registers_1_register_output_2, shifter_2_out, shifter_3_out, TagastusAadress;

  or or_1 (or_1_out, mret, Katkestus);
  Multiplexer #(.width(32)) multiplexer_1 (
    .in0(adder_1_out), .in1(ALU_valjund), .out(TagastusAadress), .sel(Instruction_decoder_1_pc_controll[0]));
  not not_1 (not_1_out, Instruction_decoder_1_pc_controll[1]);
  Multiplexer #(.width(32)) multiplexer_2 (
    .in0(TagastusAadress), .in1(KatkestuseAadress), .out(multiplexer_2_out), .sel(or_1_out));
  Register #(.width(32)) PC (.D(multiplexer_2_out), .en(or_2_out), .clk(clk), .Q(juhise_aadress), .clr(reset));
  or or_2 (or_2_out, or_1_out, not_1_out);
  Multiplexer #(.width(32)) multiplexer_3 (
    .in0(32'h4), .in1(Instruction_decoder_1_immidiate), .out(multiplexer_3_out), .sel(and_1_out));
  and and_1 (and_1_out, Instruction_decoder_1_pc_controll[2], multiplexer_4_out);
  Adder #(.width(32)) adder_1 (.a(multiplexer_3_out), .b(juhise_aadress), .out(adder_1_out));  // open: cin, cout
  or or_3 (VJKA, juhise_aadress[0], juhise_aadress[1]);
  Multiplexer multiplexer_4 (
    .in0(or_4_out), .in1(not_2_out), .out(multiplexer_4_out), .sel(Instruction_decoder_1_branch_select));
  not not_2 (not_2_out, or_4_out);
  S_R_Flip_Flop s_r_ff_1 (.R(and_11_out), .clk(clk), .Q(s_r_ff_1_q), .preset(Ext_Interrupt[0]));  // open: S, reset, Qn
  S_R_Flip_Flop s_r_ff_2 (.R(and_12_out), .clk(clk), .Q(s_r_ff_2_q), .preset(Ext_Interrupt[1]));  // open: S, reset, Qn
  S_R_Flip_Flop s_r_ff_3 (.R(and_13_out), .clk(clk), .Q(s_r_ff_3_q), .preset(Ext_Interrupt[2]));  // open: S, reset, Qn
  or or_4 (or_4_out, ALU_valjund[31], ALU_valjund[30], ALU_valjund[29], ALU_valjund[28], ALU_valjund[27], ALU_valjund[26], ALU_valjund[25], ALU_valjund[24], ALU_valjund[23], ALU_valjund[22], ALU_valjund[21], ALU_valjund[20], ALU_valjund[19], ALU_valjund[18], ALU_valjund[17], ALU_valjund[16], ALU_valjund[14], ALU_valjund[13], ALU_valjund[12], ALU_valjund[11], ALU_valjund[10], ALU_valjund[9], ALU_valjund[8], ALU_valjund[7], ALU_valjund[6], ALU_valjund[5], ALU_valjund[4], ALU_valjund[3], ALU_valjund[2], ALU_valjund[1], ALU_valjund[0], ALU_valjund[15]);
  or or_5 (or_5_out, tundmatu_opcode, reset);
  or or_6 (or_6_out, or_5_out, and_2_out);
  or or_7 (or_7_out, or_6_out, and_3_out);
  or or_8 (or_8_out, or_7_out, and_4_out);
  or or_9 (or_9_out, or_8_out, and_5_out);
  or or_10 (or_10_out, or_9_out, and_6_out);
  or or_11 (or_11_out, or_10_out, and_7_out);
  or or_12 (or_12_out, or_11_out, and_8_out);
  or or_13 (or_13_out, or_12_out, and_9_out);
  or or_14 (or_14_out, or_13_out, and_10_out);
  or or_15 (or_15_out, or_14_out, and_11_out);
  or or_16 (or_16_out, or_15_out, and_12_out);
  or or_17 (or_17_out, or_16_out, and_13_out);
  or or_18 (or_18_out, or_17_out, and_14_out);
  or or_19 (or_19_out, or_18_out, and_15_out);
  or or_20 (or_20_out, or_19_out, and_16_out);
  or or_21 (or_21_out, or_20_out, and_17_out);
  or or_22 (or_22_out, or_21_out, and_18_out);
  or or_23 (or_23_out, or_22_out, and_19_out);
  or or_24 (or_24_out, or_23_out, and_20_out);
  or or_25 (or_25_out, or_24_out, and_21_out);
  or or_26 (or_26_out, or_25_out, and_22_out);
  or or_27 (or_27_out, or_26_out, and_23_out);
  or or_28 (or_28_out, or_27_out, and_24_out);
  or or_29 (or_29_out, or_28_out, and_25_out);
  or or_30 (or_30_out, or_29_out, and_26_out);
  or or_31 (or_31_out, or_30_out, and_27_out);
  or or_32 (or_32_out, or_31_out, and_28_out);
  or or_33 (or_33_out, or_32_out, and_29_out);
  or or_34 (or_34_out, or_33_out, and_30_out);
  and and_2 (and_2_out, ~or_5_out, VJKA);  // AND_Gate
  and and_3 (and_3_out, ~or_6_out, 1'b0);  // AND_Gate
  and and_4 (and_4_out, ~or_7_out, 1'b0);  // AND_Gate
  and and_5 (and_5_out, ~or_8_out, 1'b0);  // AND_Gate
  and and_6 (and_6_out, ~or_9_out, 1'b0);  // AND_Gate
  and and_7 (and_7_out, ~or_10_out, 1'b0);  // AND_Gate
  and and_8 (and_8_out, ~or_11_out, 1'b0);  // AND_Gate
  and and_9 (and_9_out, ~or_12_out, 1'b0);  // AND_Gate
  and and_10 (and_10_out, ~or_13_out, 1'b0);  // AND_Gate
  and and_11 (and_11_out, ~or_14_out, s_r_ff_1_q);  // AND_Gate
  and and_12 (and_12_out, ~or_15_out, s_r_ff_2_q);  // AND_Gate
  and and_13 (and_13_out, ~or_16_out, s_r_ff_3_q);  // AND_Gate
  and and_14 (and_14_out, ~or_17_out, Ext_Interrupt[3]);  // AND_Gate
  and and_15 (and_15_out, ~or_18_out, Ext_Interrupt[4]);  // AND_Gate
  and and_16 (and_16_out, ~or_19_out, Ext_Interrupt[5]);  // AND_Gate
  and and_17 (and_17_out, ~or_20_out, Ext_Interrupt[6]);  // AND_Gate
  and and_18 (and_18_out, ~or_21_out, Ext_Interrupt[7]);  // AND_Gate
  and and_19 (and_19_out, ~or_22_out, Ext_Interrupt[8]);  // AND_Gate
  and and_20 (and_20_out, ~or_23_out, Ext_Interrupt[9]);  // AND_Gate
  and and_21 (and_21_out, ~or_24_out, Ext_Interrupt[10]);  // AND_Gate
  and and_22 (and_22_out, ~or_25_out, Ext_Interrupt[11]);  // AND_Gate
  and and_23 (and_23_out, ~or_26_out, Ext_Interrupt[12]);  // AND_Gate
  and and_24 (and_24_out, ~or_27_out, Ext_Interrupt[13]);  // AND_Gate
  and and_25 (and_25_out, ~or_28_out, Ext_Interrupt[14]);  // AND_Gate
  and and_26 (and_26_out, ~or_29_out, Ext_Interrupt[15]);  // AND_Gate
  and and_27 (and_27_out, ~or_30_out, Ext_Interrupt[16]);  // AND_Gate
  and and_28 (and_28_out, ~or_31_out, Ext_Interrupt[17]);  // AND_Gate
  and and_29 (and_29_out, ~or_32_out, Ext_Interrupt[18]);  // AND_Gate
  and and_30 (and_30_out, ~or_33_out, Ext_Interrupt[19]);  // AND_Gate
  assign controlled_buffer_1_out = or_5_out ? {32{1'b0}} : 32'bz;  // Controlled_Buffer controlled_buffer_1
  assign controlled_buffer_1_out = and_2_out ? 32'h4 : 32'bz;  // Controlled_Buffer controlled_buffer_2
  assign controlled_buffer_1_out = and_3_out ? 32'h8 : 32'bz;  // Controlled_Buffer controlled_buffer_3
  assign controlled_buffer_1_out = and_4_out ? 32'hc : 32'bz;  // Controlled_Buffer controlled_buffer_4
  assign controlled_buffer_1_out = and_5_out ? 32'h10 : 32'bz;  // Controlled_Buffer controlled_buffer_5
  assign controlled_buffer_1_out = and_6_out ? 32'h14 : 32'bz;  // Controlled_Buffer controlled_buffer_6
  assign controlled_buffer_1_out = and_7_out ? 32'h18 : 32'bz;  // Controlled_Buffer controlled_buffer_7
  assign controlled_buffer_1_out = and_8_out ? 32'h1c : 32'bz;  // Controlled_Buffer controlled_buffer_8
  assign controlled_buffer_1_out = and_9_out ? 32'h20 : 32'bz;  // Controlled_Buffer controlled_buffer_9
  assign controlled_buffer_1_out = and_10_out ? 32'h24 : 32'bz;  // Controlled_Buffer controlled_buffer_10
  assign controlled_buffer_1_out = and_11_out ? 32'h28 : 32'bz;  // Controlled_Buffer controlled_buffer_11
  assign controlled_buffer_1_out = and_12_out ? 32'h2c : 32'bz;  // Controlled_Buffer controlled_buffer_12
  assign controlled_buffer_1_out = and_13_out ? 32'h30 : 32'bz;  // Controlled_Buffer controlled_buffer_13
  assign controlled_buffer_1_out = and_14_out ? 32'h34 : 32'bz;  // Controlled_Buffer controlled_buffer_14
  assign controlled_buffer_1_out = and_15_out ? 32'h38 : 32'bz;  // Controlled_Buffer controlled_buffer_15
  assign controlled_buffer_1_out = and_16_out ? 32'h3c : 32'bz;  // Controlled_Buffer controlled_buffer_16
  assign controlled_buffer_1_out = and_17_out ? 32'h40 : 32'bz;  // Controlled_Buffer controlled_buffer_17
  assign controlled_buffer_1_out = and_18_out ? 32'h44 : 32'bz;  // Controlled_Buffer controlled_buffer_18
  assign controlled_buffer_1_out = and_19_out ? 32'h48 : 32'bz;  // Controlled_Buffer controlled_buffer_19
  assign controlled_buffer_1_out = and_20_out ? 32'h4c : 32'bz;  // Controlled_Buffer controlled_buffer_20
  assign controlled_buffer_1_out = and_21_out ? 32'h50 : 32'bz;  // Controlled_Buffer controlled_buffer_21
  assign controlled_buffer_1_out = and_22_out ? 32'h54 : 32'bz;  // Controlled_Buffer controlled_buffer_22
  assign controlled_buffer_1_out = and_23_out ? 32'h58 : 32'bz;  // Controlled_Buffer controlled_buffer_23
  assign controlled_buffer_1_out = and_24_out ? 32'h5c : 32'bz;  // Controlled_Buffer controlled_buffer_24
  assign controlled_buffer_1_out = and_25_out ? 32'h60 : 32'bz;  // Controlled_Buffer controlled_buffer_25
  assign controlled_buffer_1_out = and_26_out ? 32'h64 : 32'bz;  // Controlled_Buffer controlled_buffer_26
  assign controlled_buffer_1_out = and_27_out ? 32'h68 : 32'bz;  // Controlled_Buffer controlled_buffer_27
  assign controlled_buffer_1_out = and_28_out ? 32'h6c : 32'bz;  // Controlled_Buffer controlled_buffer_28
  assign controlled_buffer_1_out = and_29_out ? 32'h70 : 32'bz;  // Controlled_Buffer controlled_buffer_29
  assign controlled_buffer_1_out = and_30_out ? 32'h74 : 32'bz;  // Controlled_Buffer controlled_buffer_30
  Instruction_decoder Instruction_decoder_1 (
    .Juhis(juhis), .Immidiate(Instruction_decoder_1_immidiate), .Command(Instruction_decoder_1_command),
    .Register_mux(Instruction_decoder_1_register_mux), .ALU_src_A(Instruction_decoder_1_alu_src_a),
    .rs1(Instruction_decoder_1_rs1), .rs2(Instruction_decoder_1_rs2), .rd(Instruction_decoder_1_rd),
    .Data_type(Instruction_decoder_1_data_type), .ALU_src_B(Instruction_decoder_1_alu_src_b),
    .Write_enable(kirjuta_mallu), .CSR_write_enable(kirjutaCSR), .CSR_address(CSRaadress), .mret(mret),
    .Branch_select(Instruction_decoder_1_branch_select), .PC_controll(Instruction_decoder_1_pc_controll),
    .kehtiv_opcode(Instruction_decoder_1_kehtiv_opcode));
  or or_35 (Katkestus, or_5_out, and_31_out);
  and and_31 (and_31_out, or_36_out, MIE);
  or or_36 (or_36_out, and_2_out, or_37_out);
  or or_37 (or_37_out, and_3_out, or_38_out);
  or or_38 (or_38_out, and_4_out, or_39_out);
  or or_39 (or_39_out, and_5_out, or_40_out);
  or or_40 (or_40_out, and_6_out, or_41_out);
  or or_41 (or_41_out, and_7_out, or_42_out);
  or or_42 (or_42_out, and_8_out, or_43_out);
  or or_43 (or_43_out, and_9_out, or_44_out);
  or or_44 (or_44_out, and_10_out, or_45_out);
  or or_45 (or_45_out, and_11_out, or_46_out);
  or or_46 (or_46_out, and_12_out, or_47_out);
  or or_47 (or_47_out, and_13_out, or_48_out);
  or or_48 (or_48_out, and_14_out, or_49_out);
  or or_49 (or_49_out, and_15_out, or_50_out);
  or or_50 (or_50_out, and_16_out, or_51_out);
  or or_51 (or_51_out, and_17_out, or_52_out);
  or or_52 (or_52_out, and_18_out, or_53_out);
  or or_53 (or_53_out, and_19_out, or_54_out);
  or or_54 (or_54_out, and_20_out, or_55_out);
  or or_55 (or_55_out, and_21_out, or_56_out);
  or or_56 (or_56_out, and_22_out, or_57_out);
  or or_57 (or_57_out, and_23_out, or_58_out);
  or or_58 (or_58_out, and_24_out, or_59_out);
  or or_59 (or_59_out, and_25_out, or_60_out);
  or or_60 (or_60_out, and_26_out, or_61_out);
  or or_61 (or_61_out, and_27_out, or_62_out);
  or or_62 (or_62_out, and_28_out, or_63_out);
  or or_63 (or_63_out, and_29_out, or_64_out);
  or or_64 (or_64_out, and_30_out, or_34_out);
  not not_3 (tundmatu_opcode, Instruction_decoder_1_kehtiv_opcode);
  assign KatkestuseAadress = Katkestus ? controlled_buffer_1_out : 32'bz;  // Controlled_Buffer controlled_buffer_31
  and and_32 (and_32_out, ~undriven_2, undriven);  // AND_Gate
  or or_65 (or_65_out, undriven_2, and_32_out);
  assign controlled_buffer_32_out = and_32_out ? 32'h20 : 32'bz;  // Controlled_Buffer controlled_buffer_32
  // OR_Gate or_66 has open pins: in0=and_32_out, in1=undriven_3, out=open
  Registers Registers_1 (
    .Read_address_2(Instruction_decoder_1_rs2), .Read_address_1(Instruction_decoder_1_rs1),
    .Data_in(multiplexer_11_out), .Write_address(Instruction_decoder_1_rd), .Clock(clk),
    .Register_output_2(Registers_1_register_output_2), .Register_output_1(Registers_1_register_output_1));  // open: Reset
  Multiplexer #(.width(32)) multiplexer_5 (
    .in0(juhise_aadress), .in1(Registers_1_register_output_1), .out(multiplexer_5_out),
    .sel(Instruction_decoder_1_alu_src_a));
  Multiplexer #(.width(32)) multiplexer_6 (
    .in0(Registers_1_register_output_2), .in1(Instruction_decoder_1_immidiate), .out(multiplexer_6_out),
    .sel(Instruction_decoder_1_alu_src_b));
  ALU_RV32I ALU (
    .Juhend(Instruction_decoder_1_command), .a1(multiplexer_5_out), .a2(multiplexer_6_out),
    .Tulemus(ALU_valjund));
  Comparator #(.mode("unsigned"), .width(12)) comparator_1 (
    .a(CSRaadress), .b(12'h301), .eq(comparator_1_eq));  // open: gt, lt
  Comparator #(.mode("unsigned"), .width(12)) comparator_2 (
    .a(CSRaadress), .b({12{1'b0}}), .eq(comparator_2_eq));  // open: gt, lt
  Comparator #(.mode("unsigned"), .width(12)) comparator_3 (
    .a(CSRaadress), .b(12'hf12), .eq(comparator_3_eq));  // open: gt, lt
  Comparator #(.mode("unsigned"), .width(12)) comparator_4 (
    .a(CSRaadress), .b(12'hf13), .eq(comparator_4_eq));  // open: gt, lt
  Comparator #(.mode("unsigned"), .width(12)) comparator_5 (
    .a(CSRaadress), .b(12'hf14), .eq(comparator_5_eq));  // open: gt, lt
  Comparator #(.mode("unsigned"), .width(12)) comparator_6 (
    .a(CSRaadress), .b(12'h341), .eq(comparator_6_eq));  // open: gt, lt
  Comparator #(.mode("unsigned"), .width(12)) comparator_7 (
    .a(CSRaadress), .b(12'hb00), .eq(comparator_7_eq));  // open: gt, lt
  Comparator #(.mode("unsigned"), .width(12)) comparator_8 (
    .a(CSRaadress), .b(12'h300), .eq(comparator_8_eq));  // open: gt, lt
  and and_33 (and_33_out, comparator_6_eq, kirjutaCSR);
  and and_34 (and_34_out, comparator_8_eq, kirjutaCSR);
  Multiplexer #(.select(3), .width(32)) multiplexer_7 (
    .in5(Registers_1_register_output_2), .in6({{16{1'b0}}, Registers_1_register_output_2[15:0]}),
    .in7({{24{1'b0}}, Registers_1_register_output_2[7:0]}), .out(multiplexer_7_out),
    .sel(Instruction_decoder_1_data_type));  // open: in0, in1, in2, in3, in4
  Multiplexer #(.select(3), .width(4)) multiplexer_8 (
    .in5(4'b1111), .in6(4'b0011), .in7(4'b0001), .out(multiplexer_8_out),
    .sel(Instruction_decoder_1_data_type));  // open: in0, in1, in2, in3, in4
  Multiplexer #(.width(32)) multiplexer_9 (
    .in0(ALU_valjund), .in1(TagastusAadress), .out(multiplexer_9_out), .sel(Katkestus));
  Multiplexer #(.width(32)) multiplexer_10 (
    .in0(ALU_valjund), .in1({register_2_q[29:16], 1'b0, register_2_q[15:3], 1'b0, register_2_q[2:0]}),
    .out(multiplexer_10_out), .sel(reset));
  Shifter #(.width(4)) shifter_1 (.in(multiplexer_8_out), .\dist (ALU_valjund[1:0]), .out(shifter_1_out));
  Register #(.width(30)) register_1 (
    .D(multiplexer_9_out[31:2]), .en(or_67_out), .clk(clk), .Q(register_1_q));  // open: clr
  or or_67 (or_67_out, Katkestus, and_33_out);
  Register #(.width(32)) register_2 (
    .D(multiplexer_10_out), .en(or_68_out), .clk(clk),
    .Q({register_2_q[29:16], register_2_q_2[17], register_2_q[15:3], MIE, register_2_q[2:0]}));  // open: clr
  or or_68 (or_68_out, reset, and_34_out);
  // Probe on ALU_valjund
  Shifter #(.width(32)) shifter_2 (.in(multiplexer_7_out), .\dist ({ALU_valjund[1:0], 3'b000}), .out(shifter_2_out));
  assign not_4_out = ~{{8{shifter_1_out[3]}}, {8{shifter_1_out[2]}}, {8{shifter_1_out[1]}}, {8{shifter_1_out[0]}}};  // NOT_Gate not_4, 32 bits wide
  assign and_35_out = malu_sisend & not_4_out;  // AND_Gate and_35, 32 bits wide
  Counter #(.max('hffffffff), .width(32)) counter_1 (
    .count(1'b1), .Q(counter_1_q), .up(1'b1), .clk(clk));  // open: load, D, carry, clr
  assign or_69_out = shifter_2_out | and_35_out;  // OR_Gate or_69, 32 bits wide
  assign malu_valjund = kirjuta_mallu ? or_69_out : 32'bz;  // Controlled_Buffer controlled_buffer_33
  assign CSRvaljund = comparator_1_eq ? 32'h80000100 : 32'bz;  // Controlled_Buffer controlled_buffer_34
  assign CSRvaljund = comparator_2_eq ? {32{1'b0}} : 32'bz;  // Controlled_Buffer controlled_buffer_35
  assign CSRvaljund = comparator_3_eq ? {32{1'b0}} : 32'bz;  // Controlled_Buffer controlled_buffer_36
  assign CSRvaljund = comparator_4_eq ? {32{1'b0}} : 32'bz;  // Controlled_Buffer controlled_buffer_37
  assign CSRvaljund = comparator_5_eq ? {32{1'b0}} : 32'bz;  // Controlled_Buffer controlled_buffer_38
  assign CSRvaljund = comparator_6_eq ? {register_1_q, 2'b00} : 32'bz;  // Controlled_Buffer controlled_buffer_39
  assign KatkestuseAadress = mret ? {register_1_q, 2'b00} : 32'bz;  // Controlled_Buffer controlled_buffer_40
  assign CSRvaljund = comparator_7_eq ? counter_1_q : 32'bz;  // Controlled_Buffer controlled_buffer_41
  assign CSRvaljund = comparator_8_eq ? {register_2_q[29:16], register_2_q_2[17], register_2_q[15:3], MIE, register_2_q[2:0]} : 32'bz;  // Controlled_Buffer controlled_buffer_42
  Shifter #(.shift("lr"), .width(32)) shifter_3 (
    .in(malu_sisend), .\dist ({ALU_valjund[1:0], 3'b000}), .out(shifter_3_out));
  assign bit_extender_1_out = {{16{shifter_3_out[15]}}, shifter_3_out[15:0]};  // Bit_Extender bit_extender_1
  assign bit_extender_2_out = {{16{1'b0}}, shifter_3_out[15:0]};  // Bit_Extender bit_extender_2
  assign bit_extender_3_out = {{24{shifter_3_out[7]}}, shifter_3_out[7:0]};  // Bit_Extender bit_extender_3
  assign bit_extender_4_out = {{24{1'b0}}, shifter_3_out[7:0]};  // Bit_Extender bit_extender_4
  Multiplexer #(.select(2), .width(32)) multiplexer_11 (
    .in0(adder_1_out), .in1(CSRvaljund), .in2(ALU_valjund), .in3(multiplexer_12_out),
    .out(multiplexer_11_out), .sel(Instruction_decoder_1_register_mux));
  Multiplexer #(.select(3), .width(32)) multiplexer_12 (
    .in0(shifter_3_out), .in1(bit_extender_1_out), .in2(bit_extender_2_out), .in3(bit_extender_3_out),
    .in4(bit_extender_4_out), .out(multiplexer_12_out), .sel(Instruction_decoder_1_data_type));  // open: in5, in6, in7

  // Other names for the same wires on the sheet: ALUvaljund[31:0] = ALU_valjund

  // Notes on the sheet:
  //   malu_valjund: pull=down
endmodule

module ALU (
  input  [4:0] Juhend,
  input  [31:0] a1,
  input  [31:0] a2,
  output [31:0] Tulemus
);

  wire adder_1_cout, comparator_1_lt, decoder_1_out1, decoder_1_out2, decoder_1_out12, decoder_1_out13,
       not_1_out, or_1_out, or_2_out;
  wire [31:0] adder_1_out, and_1_out, bit_extender_1_out, bit_extender_2_out, bit_extender_3_out,
       divider_1_out, divider_1_rem, divider_2_out, divider_2_rem, Korrutaja_1_carry, Korrutaja_1_result,
       or_3_out, shifter_1_out, shifter_2_out, shifter_3_out, xor_1_out, xor_2_out;

  Decoder #(.enable("false"), .select(5)) decoder_1 (
    .out1(decoder_1_out1), .out2(decoder_1_out2), .out12(decoder_1_out12), .out13(decoder_1_out13),
    .sel(Juhend));  // open: out0, out3, out4, out5, out6, out7, out8, out9, out10, out11, out14, out15, out16, out17, out18, out19, out20, out21, out22, out23, out24, out25, out26, out27, out28, out29, out30, out31
  or or_1 (or_1_out, decoder_1_out1, decoder_1_out2);
  assign bit_extender_1_out = {{31{or_1_out}}, or_1_out};  // Bit_Extender bit_extender_1
  or or_2 (or_2_out, decoder_1_out13, decoder_1_out12);
  assign xor_1_out = bit_extender_1_out ^ a2;  // XOR_Gate xor_1, 32 bits wide
  Adder #(.width(32)) adder_1 (.a(a1), .b(xor_1_out), .out(adder_1_out), .cin(or_1_out), .cout(adder_1_cout));
  not not_1 (not_1_out, adder_1_cout);
  Shifter #(.width(32)) shifter_1 (.in(a1), .\dist (a2[4:0]), .out(shifter_1_out));
  Shifter #(.shift("lr"), .width(32)) shifter_2 (.in(a1), .\dist (a2[4:0]), .out(shifter_2_out));
  Shifter #(.shift("ar"), .width(32)) shifter_3 (.in(a1), .\dist (a2[4:0]), .out(shifter_3_out));
  assign and_1_out = a1 & a2;  // AND_Gate and_1, 32 bits wide
  assign or_3_out = a1 | a2;  // OR_Gate or_3, 32 bits wide
  assign xor_2_out = a1 ^ a2;  // XOR_Gate xor_2, 32 bits wide
  Comparator #(.width(32)) comparator_1 (.b(a2), .lt(comparator_1_lt));  // open: a, gt, eq
  Divider #(.width(32)) divider_1 (.a(a1), .b(a2), .out(divider_1_out), .rem(divider_1_rem));  // open: upper
  Divider #(.mode("twosComplement"), .width(32)) divider_2 (
    .a(a1), .b(a2), .out(divider_2_out), .rem(divider_2_rem));  // open: upper
  assign bit_extender_2_out = {{31{1'b0}}, not_1_out};  // Bit_Extender bit_extender_2
  assign bit_extender_3_out = {{31{1'b0}}, comparator_1_lt};  // Bit_Extender bit_extender_3
  Korrutaja Korrutaja_1 (
    .a_signed(or_2_out), .a(a1), .b_signed(decoder_1_out12), .b(a2), .result(Korrutaja_1_result),
    .carry(Korrutaja_1_carry));
  Multiplexer #(.select(5), .width(32)) multiplexer_1 (
    .in0(adder_1_out), .in1(adder_1_out), .in2(bit_extender_2_out), .in3(shifter_1_out), .in4(shifter_2_out),
    .in5(shifter_3_out), .in6(and_1_out), .in7(or_3_out), .in8(xor_2_out), .in9(bit_extender_3_out),
    .in10(Korrutaja_1_result), .in11(Korrutaja_1_carry), .in12(Korrutaja_1_carry), .in13(Korrutaja_1_carry),
    .in14(divider_1_out), .in15(divider_1_rem), .in16(divider_2_out), .in17(divider_2_rem), .out(Tulemus),
    .sel(Juhend));  // open: in18, in19, in20, in21, in22, in23, in24, in25, in26, in27, in28, in29, in30, in31

  // Notes on the sheet:
  //   Liida/Lahuta
  //   Add/Subtract
  //   Loogiline vasaknihutus
  //   Logical shift left
  //   Loogiline paremnihutus
  //   Logical shift right
  //   Aritmeetiline paremnihutus
  //   Arithmetic right shift
  //   AND värav
  //   AND gate
  //   OR värav
  //   OR gate
  //   XOR värav
  //   XOR gate
endmodule

module Registers (
  input  [4:0] Read_address_1,
  input  [31:0] Data_in,
  input  Reset,
  input  Clock,
  input  [4:0] Read_address_2,
  input  [4:0] Write_address,
  output [31:0] Register_output_1,
  output [31:0] Register_output_2
);

  wire decoder_1_out1, decoder_1_out2, decoder_1_out3, decoder_1_out4, decoder_1_out5, decoder_1_out6,
       decoder_1_out7, decoder_1_out8, decoder_1_out9, decoder_1_out10, decoder_1_out11, decoder_1_out12,
       decoder_1_out13, decoder_1_out14, decoder_1_out15, decoder_1_out16, decoder_1_out17, decoder_1_out18,
       decoder_1_out19, decoder_1_out20, decoder_1_out21, decoder_1_out22, decoder_1_out23, decoder_1_out24,
       decoder_1_out25, decoder_1_out26, decoder_1_out27, decoder_1_out28, decoder_1_out29, decoder_1_out30,
       decoder_1_out31;
  wire [31:0] X1_q, X2_q, X3_q, X4_q, X5_q, X6_q, X7_q, X8_q, X9_q, X10_q, X11_q, X12_q, X13_q, X14_q, X15_q,
       X16_q, X17_q, X18_q, X19_q, X20_q, X21_q, X22_q, X23_q, X24_q, X25_q, X26_q, X27_q, X28_q, X29_q,
       X30_q, X31_q;

  Decoder #(.enable("false"), .select(5)) decoder_1 (
    .out1(decoder_1_out1), .out2(decoder_1_out2), .out3(decoder_1_out3), .out4(decoder_1_out4),
    .out5(decoder_1_out5), .out6(decoder_1_out6), .out7(decoder_1_out7), .out8(decoder_1_out8),
    .out9(decoder_1_out9), .out10(decoder_1_out10), .out11(decoder_1_out11), .out12(decoder_1_out12),
    .out13(decoder_1_out13), .out14(decoder_1_out14), .out15(decoder_1_out15), .out16(decoder_1_out16),
    .out17(decoder_1_out17), .out18(decoder_1_out18), .out19(decoder_1_out19), .out20(decoder_1_out20),
    .out21(decoder_1_out21), .out22(decoder_1_out22), .out23(decoder_1_out23), .out24(decoder_1_out24),
    .out25(decoder_1_out25), .out26(decoder_1_out26), .out27(decoder_1_out27), .out28(decoder_1_out28),
    .out29(decoder_1_out29), .out30(decoder_1_out30), .out31(decoder_1_out31), .sel(Write_address));  // open: out0
  Register #(.width(32)) X28 (.D(Data_in), .en(decoder_1_out28), .clk(Clock), .Q(X28_q), .clr(Reset));
  Register #(.width(32)) X29 (.D(Data_in), .en(decoder_1_out29), .clk(Clock), .Q(X29_q), .clr(Reset));
  Register #(.width(32)) X30 (.D(Data_in), .en(decoder_1_out30), .clk(Clock), .Q(X30_q), .clr(Reset));
  Register #(.width(32)) X31 (.D(Data_in), .en(decoder_1_out31), .clk(Clock), .Q(X31_q), .clr(Reset));
  Register #(.width(32)) X24 (.D(Data_in), .en(decoder_1_out24), .clk(Clock), .Q(X24_q), .clr(Reset));
  Register #(.width(32)) X25 (.D(Data_in), .en(decoder_1_out25), .clk(Clock), .Q(X25_q), .clr(Reset));
  Register #(.width(32)) X26 (.D(Data_in), .en(decoder_1_out26), .clk(Clock), .Q(X26_q), .clr(Reset));
  Register #(.width(32)) X27 (.D(Data_in), .en(decoder_1_out27), .clk(Clock), .Q(X27_q), .clr(Reset));
  Register #(.width(32)) X20 (.D(Data_in), .en(decoder_1_out20), .clk(Clock), .Q(X20_q), .clr(Reset));
  Register #(.width(32)) X21 (.D(Data_in), .en(decoder_1_out21), .clk(Clock), .Q(X21_q), .clr(Reset));
  Register #(.width(32)) X22 (.D(Data_in), .en(decoder_1_out22), .clk(Clock), .Q(X22_q), .clr(Reset));
  Register #(.width(32)) X23 (.D(Data_in), .en(decoder_1_out23), .clk(Clock), .Q(X23_q), .clr(Reset));
  Register #(.width(32)) X16 (.D(Data_in), .en(decoder_1_out16), .clk(Clock), .Q(X16_q), .clr(Reset));
  Register #(.width(32)) X17 (.D(Data_in), .en(decoder_1_out17), .clk(Clock), .Q(X17_q), .clr(Reset));
  Register #(.width(32)) X18 (.D(Data_in), .en(decoder_1_out18), .clk(Clock), .Q(X18_q), .clr(Reset));
  Register #(.width(32)) X19 (.D(Data_in), .en(decoder_1_out19), .clk(Clock), .Q(X19_q), .clr(Reset));
  Register #(.width(32)) X12 (.D(Data_in), .en(decoder_1_out12), .clk(Clock), .Q(X12_q), .clr(Reset));
  Register #(.width(32)) X13 (.D(Data_in), .en(decoder_1_out13), .clk(Clock), .Q(X13_q), .clr(Reset));
  Register #(.width(32)) X14 (.D(Data_in), .en(decoder_1_out14), .clk(Clock), .Q(X14_q), .clr(Reset));
  Register #(.width(32)) X15 (.D(Data_in), .en(decoder_1_out15), .clk(Clock), .Q(X15_q), .clr(Reset));
  Register #(.width(32)) X8 (.D(Data_in), .en(decoder_1_out8), .clk(Clock), .Q(X8_q), .clr(Reset));
  Register #(.width(32)) X9 (.D(Data_in), .en(decoder_1_out9), .clk(Clock), .Q(X9_q), .clr(Reset));
  Register #(.width(32)) X10 (.D(Data_in), .en(decoder_1_out10), .clk(Clock), .Q(X10_q), .clr(Reset));
  Register #(.width(32)) X11 (.D(Data_in), .en(decoder_1_out11), .clk(Clock), .Q(X11_q), .clr(Reset));
  Register #(.width(32)) X4 (.D(Data_in), .en(decoder_1_out4), .clk(Clock), .Q(X4_q), .clr(Reset));
  Register #(.width(32)) X5 (.D(Data_in), .en(decoder_1_out5), .clk(Clock), .Q(X5_q), .clr(Reset));
  Register #(.width(32)) X6 (.D(Data_in), .en(decoder_1_out6), .clk(Clock), .Q(X6_q), .clr(Reset));
  Register #(.width(32)) X7 (.D(Data_in), .en(decoder_1_out7), .clk(Clock), .Q(X7_q), .clr(Reset));
  Register #(.width(32)) X1 (.D(Data_in), .en(decoder_1_out1), .clk(Clock), .Q(X1_q), .clr(Reset));
  Register #(.width(32)) X2 (.D(Data_in), .en(decoder_1_out2), .clk(Clock), .Q(X2_q), .clr(Reset));
  Register #(.width(32)) X3 (.D(Data_in), .en(decoder_1_out3), .clk(Clock), .Q(X3_q), .clr(Reset));
  Multiplexer #(.select(5), .width(32)) multiplexer_1 (
    .in0({32{1'b0}}), .in1(X1_q), .in2(X2_q), .in3(X3_q), .in4(X4_q), .in5(X5_q), .in6(X6_q), .in7(X7_q),
    .in8(X8_q), .in9(X9_q), .in10(X10_q), .in11(X11_q), .in12(X12_q), .in13(X13_q), .in14(X14_q),
    .in15(X15_q), .in16(X16_q), .in17(X17_q), .in18(X18_q), .in19(X19_q), .in20(X20_q), .in21(X21_q),
    .in22(X22_q), .in23(X23_q), .in24(X24_q), .in25(X25_q), .in26(X26_q), .in27(X27_q), .in28(X28_q),
    .in29(X29_q), .in30(X30_q), .in31(X31_q), .out(Register_output_1), .sel(Read_address_1));
  Multiplexer #(.select(5), .width(32)) multiplexer_2 (
    .in0({32{1'b0}}), .in1(X1_q), .in2(X2_q), .in3(X3_q), .in4(X4_q), .in5(X5_q), .in6(X6_q), .in7(X7_q),
    .in8(X8_q), .in9(X9_q), .in10(X10_q), .in11(X11_q), .in12(X12_q), .in13(X13_q), .in14(X14_q),
    .in15(X15_q), .in16(X16_q), .in17(X17_q), .in18(X18_q), .in19(X19_q), .in20(X20_q), .in21(X21_q),
    .in22(X22_q), .in23(X23_q), .in24(X24_q), .in25(X25_q), .in26(X26_q), .in27(X27_q), .in28(X28_q),
    .in29(X29_q), .in30(X30_q), .in31(X31_q), .out(Register_output_2), .sel(Read_address_2));

  // Notes on the sheet:
  //   X0
endmodule

module Instruction_decoder (
  input  [31:0] Juhis,
  output [31:0] Immidiate,
  output [4:0] Command,
  output [1:0] Register_mux,
  output ALU_src_A,
  output [4:0] rs1,
  output [4:0] rs2,
  output [4:0] rd,
  output [2:0] Data_type,
  output ALU_src_B,
  output Write_enable,
  output CSR_write_enable,
  output [11:0] CSR_address,
  output mret,
  output Branch_select,
  output [2:0] PC_controll,
  output kehtiv_opcode
);

  wire and_1_out, and_2_out, and_3_out, and_4_out, and_5_out, and_6_out, and_7_out, and_8_out, and_9_out,
       and_10_out, and_11_out, and_12_out, and_13_out, and_14_out, and_15_out, and_16_out, and_17_out,
       and_18_out, and_19_out, and_20_out, and_21_out, and_22_out, and_23_out, and_24_out, and_25_out,
       and_26_out, and_27_out, and_28_out, and_29_out, and_30_out, and_31_out, and_32_out, and_33_out,
       and_34_out, and_35_out, and_36_out, and_37_out, and_38_out, and_39_out, and_40_out, and_41_out,
       and_42_out, and_43_out, and_44_out, and_45_out, and_46_out, and_47_out, and_48_out, and_49_out,
       and_50_out, and_51_out, and_52_out, and_53_out, and_54_out, and_55_out, and_56_out, and_57_out,
       and_58_out, and_59_out, and_60_out, and_61_out, and_62_out, and_63_out, and_64_out, or_1_out;
  wire [11:0] bit_extender_3_out;
  wire [31:0] bit_extender_1_out, bit_extender_2_out, bit_extender_4_out, bit_extender_5_out,
       bit_extender_6_out, bit_extender_7_out;

  and and_1 (and_1_out, Juhis[0], Juhis[1], ~Juhis[2], ~Juhis[3], Juhis[4], Juhis[5], ~Juhis[6]);  // AND_Gate
  and and_2 (and_2_out, Juhis[0], Juhis[1], ~Juhis[2], ~Juhis[3], Juhis[4], Juhis[5], ~Juhis[6], ~Juhis[12], ~Juhis[13], ~Juhis[14], ~Juhis[25], ~Juhis[26], ~Juhis[27], ~Juhis[28], ~Juhis[29], ~Juhis[30], ~Juhis[31]);  // AND_Gate
  and and_3 (and_3_out, Juhis[0], Juhis[1], ~Juhis[2], ~Juhis[3], Juhis[4], Juhis[5], ~Juhis[6], ~Juhis[12], ~Juhis[13], ~Juhis[14], ~Juhis[25], ~Juhis[26], ~Juhis[27], ~Juhis[28], ~Juhis[29], Juhis[30], ~Juhis[31]);  // AND_Gate
  and and_4 (and_4_out, Juhis[0], Juhis[1], ~Juhis[2], ~Juhis[3], Juhis[4], Juhis[5], ~Juhis[6], Juhis[12], Juhis[13], Juhis[14], ~Juhis[25], ~Juhis[26], ~Juhis[27], ~Juhis[28], ~Juhis[29], ~Juhis[30], ~Juhis[31]);  // AND_Gate
  and and_5 (and_5_out, Juhis[0], Juhis[1], ~Juhis[2], ~Juhis[3], Juhis[4], Juhis[5], ~Juhis[6], ~Juhis[12], Juhis[13], Juhis[14], ~Juhis[25], ~Juhis[26], ~Juhis[27], ~Juhis[28], ~Juhis[29], ~Juhis[30], ~Juhis[31]);  // AND_Gate
  and and_6 (and_6_out, Juhis[0], Juhis[1], ~Juhis[2], ~Juhis[3], Juhis[4], Juhis[5], ~Juhis[6], ~Juhis[12], ~Juhis[13], Juhis[14], ~Juhis[25], ~Juhis[26], ~Juhis[27], ~Juhis[28], ~Juhis[29], ~Juhis[30], ~Juhis[31]);  // AND_Gate
  and and_7 (and_7_out, Juhis[0], Juhis[1], ~Juhis[2], ~Juhis[3], Juhis[4], Juhis[5], ~Juhis[6], Juhis[12], ~Juhis[13], ~Juhis[14], ~Juhis[25], ~Juhis[26], ~Juhis[27], ~Juhis[28], ~Juhis[29], ~Juhis[30], ~Juhis[31]);  // AND_Gate
  and and_8 (and_8_out, Juhis[0], Juhis[1], ~Juhis[2], ~Juhis[3], Juhis[4], Juhis[5], ~Juhis[6], ~Juhis[12], Juhis[13], ~Juhis[14], ~Juhis[25], ~Juhis[26], ~Juhis[27], ~Juhis[28], ~Juhis[29], ~Juhis[30], ~Juhis[31]);  // AND_Gate
  and and_9 (and_9_out, Juhis[0], Juhis[1], ~Juhis[2], ~Juhis[3], Juhis[4], Juhis[5], ~Juhis[6], Juhis[12], Juhis[13], ~Juhis[14], ~Juhis[25], ~Juhis[26], ~Juhis[27], ~Juhis[28], ~Juhis[29], ~Juhis[30], ~Juhis[31]);  // AND_Gate
  and and_10 (and_10_out, Juhis[0], Juhis[1], ~Juhis[2], ~Juhis[3], Juhis[4], Juhis[5], ~Juhis[6], Juhis[12], Juhis[13], ~Juhis[14], ~Juhis[25], ~Juhis[26], ~Juhis[27], ~Juhis[28], ~Juhis[29], ~Juhis[30], ~Juhis[31]);  // AND_Gate
  and and_11 (and_11_out, Juhis[0], Juhis[1], ~Juhis[2], ~Juhis[3], Juhis[4], Juhis[5], ~Juhis[6], Juhis[12], Juhis[13], ~Juhis[14], ~Juhis[25], ~Juhis[26], ~Juhis[27], ~Juhis[28], ~Juhis[29], Juhis[30], ~Juhis[31]);  // AND_Gate
  and and_12 (and_12_out, Juhis[0], Juhis[1], ~Juhis[2], ~Juhis[3], Juhis[4], Juhis[5], ~Juhis[6], ~Juhis[12], ~Juhis[13], ~Juhis[14], Juhis[25], ~Juhis[26], ~Juhis[27], ~Juhis[28], ~Juhis[29], ~Juhis[30], ~Juhis[31]);  // AND_Gate
  and and_13 (and_13_out, Juhis[0], Juhis[1], ~Juhis[2], ~Juhis[3], Juhis[4], Juhis[5], ~Juhis[6], Juhis[12], ~Juhis[13], ~Juhis[14], Juhis[25], ~Juhis[26], ~Juhis[27], ~Juhis[28], ~Juhis[29], ~Juhis[30], ~Juhis[31]);  // AND_Gate
  and and_14 (and_14_out, Juhis[0], Juhis[1], ~Juhis[2], ~Juhis[3], Juhis[4], Juhis[5], ~Juhis[6], Juhis[12], Juhis[13], ~Juhis[14], Juhis[25], ~Juhis[26], ~Juhis[27], ~Juhis[28], ~Juhis[29], ~Juhis[30], ~Juhis[31]);  // AND_Gate
  and and_15 (and_15_out, Juhis[0], Juhis[1], ~Juhis[2], ~Juhis[3], Juhis[4], Juhis[5], ~Juhis[6], ~Juhis[12], Juhis[13], ~Juhis[14], Juhis[25], ~Juhis[26], ~Juhis[27], ~Juhis[28], ~Juhis[29], ~Juhis[30], ~Juhis[31]);  // AND_Gate
  and and_16 (and_16_out, Juhis[0], Juhis[1], ~Juhis[2], ~Juhis[3], Juhis[4], Juhis[5], ~Juhis[6], Juhis[12], ~Juhis[13], Juhis[14], Juhis[25], ~Juhis[26], ~Juhis[27], ~Juhis[28], ~Juhis[29], ~Juhis[30], ~Juhis[31]);  // AND_Gate
  and and_17 (and_17_out, Juhis[0], Juhis[1], ~Juhis[2], ~Juhis[3], Juhis[4], Juhis[5], ~Juhis[6], Juhis[12], Juhis[13], Juhis[14], Juhis[25], ~Juhis[26], ~Juhis[27], ~Juhis[28], ~Juhis[29], ~Juhis[30], ~Juhis[31]);  // AND_Gate
  and and_18 (and_18_out, Juhis[0], Juhis[1], ~Juhis[2], ~Juhis[3], Juhis[4], Juhis[5], ~Juhis[6], ~Juhis[12], ~Juhis[13], Juhis[14], Juhis[25], ~Juhis[26], ~Juhis[27], ~Juhis[28], ~Juhis[29], ~Juhis[30], ~Juhis[31]);  // AND_Gate
  and and_19 (and_19_out, Juhis[0], Juhis[1], ~Juhis[2], ~Juhis[3], Juhis[4], Juhis[5], ~Juhis[6], ~Juhis[12], Juhis[13], Juhis[14], Juhis[25], ~Juhis[26], ~Juhis[27], ~Juhis[28], ~Juhis[29], ~Juhis[30], ~Juhis[31]);  // AND_Gate
  assign rd = and_1_out ? Juhis[11:7] : 5'bz;  // Controlled_Buffer controlled_buffer_1
  assign rs1 = and_1_out ? Juhis[19:15] : 5'bz;  // Controlled_Buffer controlled_buffer_2
  assign rs2 = and_1_out ? Juhis[24:20] : 5'bz;  // Controlled_Buffer controlled_buffer_3
  assign ALU_src_B = and_1_out ? 1'b0 : 1'bz;  // Controlled_Buffer controlled_buffer_4
  assign Write_enable = and_1_out ? 1'b0 : 1'bz;  // Controlled_Buffer controlled_buffer_5
  assign ALU_src_A = and_1_out ? 1'b1 : 1'bz;  // Controlled_Buffer controlled_buffer_6
  assign Data_type = and_1_out ? 3'b000 : 3'bz;  // Controlled_Buffer controlled_buffer_7
  assign Register_mux = and_1_out ? 2'b10 : 2'bz;  // Controlled_Buffer controlled_buffer_8
  assign CSR_write_enable = and_1_out ? 1'b0 : 1'bz;  // Controlled_Buffer controlled_buffer_9
  assign CSR_address = and_1_out ? {12{1'b0}} : 12'bz;  // Controlled_Buffer controlled_buffer_10
  assign PC_controll = and_1_out ? 3'b000 : 3'bz;  // Controlled_Buffer controlled_buffer_11
  assign mret = and_1_out ? 1'b0 : 1'bz;  // Controlled_Buffer controlled_buffer_12
  assign kehtiv_opcode = and_1_out ? 1'b1 : 1'bz;  // Controlled_Buffer controlled_buffer_13
  assign Command = and_2_out ? {5{1'b0}} : 5'bz;  // Controlled_Buffer controlled_buffer_14
  assign Command = and_3_out ? 5'b00001 : 5'bz;  // Controlled_Buffer controlled_buffer_15
  assign Command = and_4_out ? 5'b00110 : 5'bz;  // Controlled_Buffer controlled_buffer_16
  assign Command = and_5_out ? 5'b00111 : 5'bz;  // Controlled_Buffer controlled_buffer_17
  assign Command = and_6_out ? 5'b01000 : 5'bz;  // Controlled_Buffer controlled_buffer_18
  assign Command = and_7_out ? 5'b00011 : 5'bz;  // Controlled_Buffer controlled_buffer_19
  assign Command = and_8_out ? 5'b01001 : 5'bz;  // Controlled_Buffer controlled_buffer_20
  assign Command = and_9_out ? 5'b00010 : 5'bz;  // Controlled_Buffer controlled_buffer_21
  assign Command = and_10_out ? 5'b00100 : 5'bz;  // Controlled_Buffer controlled_buffer_22
  assign Command = and_11_out ? 5'b00101 : 5'bz;  // Controlled_Buffer controlled_buffer_23
  assign Command = and_12_out ? 5'b01010 : 5'bz;  // Controlled_Buffer controlled_buffer_24
  assign Command = and_13_out ? 5'b01011 : 5'bz;  // Controlled_Buffer controlled_buffer_25
  assign Command = and_14_out ? 5'b01100 : 5'bz;  // Controlled_Buffer controlled_buffer_26
  assign Command = and_15_out ? 5'b01101 : 5'bz;  // Controlled_Buffer controlled_buffer_27
  assign Command = and_16_out ? 5'b01110 : 5'bz;  // Controlled_Buffer controlled_buffer_28
  assign Command = and_17_out ? 5'b01111 : 5'bz;  // Controlled_Buffer controlled_buffer_29
  assign Command = and_18_out ? 5'b10000 : 5'bz;  // Controlled_Buffer controlled_buffer_30
  assign Command = and_19_out ? 5'b10001 : 5'bz;  // Controlled_Buffer controlled_buffer_31
  and and_20 (and_20_out, Juhis[0], Juhis[1], Juhis[2], ~Juhis[3], Juhis[4], Juhis[5], ~Juhis[6]);  // AND_Gate
  and and_21 (and_21_out, Juhis[0], Juhis[1], Juhis[2], ~Juhis[3], Juhis[4], ~Juhis[5], ~Juhis[6]);  // AND_Gate
  assign rd = and_20_out ? Juhis[11:7] : 5'bz;  // Controlled_Buffer controlled_buffer_32
  assign Immidiate = and_20_out ? {Juhis[31:12], {12{1'b0}}} : 32'bz;  // Controlled_Buffer controlled_buffer_33
  assign rs1 = and_20_out ? {5{1'b0}} : 5'bz;  // Controlled_Buffer controlled_buffer_34
  assign rd = and_21_out ? Juhis[11:7] : 5'bz;  // Controlled_Buffer controlled_buffer_35
  assign Immidiate = and_21_out ? {Juhis[31:12], {12{1'b0}}} : 32'bz;  // Controlled_Buffer controlled_buffer_36
  assign rs1 = and_21_out ? {5{1'b0}} : 5'bz;  // Controlled_Buffer controlled_buffer_37
  assign rs2 = and_20_out ? {5{1'b0}} : 5'bz;  // Controlled_Buffer controlled_buffer_38
  assign Command = and_20_out ? 5'b00111 : 5'bz;  // Controlled_Buffer controlled_buffer_39
  assign Register_mux = and_20_out ? 2'b10 : 2'bz;  // Controlled_Buffer controlled_buffer_40
  assign ALU_src_B = and_20_out ? 1'b1 : 1'bz;  // Controlled_Buffer controlled_buffer_41
  assign CSR_write_enable = and_20_out ? 1'b0 : 1'bz;  // Controlled_Buffer controlled_buffer_42
  assign CSR_address = and_20_out ? {12{1'b0}} : 12'bz;  // Controlled_Buffer controlled_buffer_43
  assign PC_controll = and_20_out ? 3'b000 : 3'bz;  // Controlled_Buffer controlled_buffer_44
  assign mret = and_20_out ? 1'b0 : 1'bz;  // Controlled_Buffer controlled_buffer_45
  assign kehtiv_opcode = and_20_out ? 1'b1 : 1'bz;  // Controlled_Buffer controlled_buffer_46
  assign rs2 = and_21_out ? {5{1'b0}} : 5'bz;  // Controlled_Buffer controlled_buffer_47
  assign Command = and_21_out ? 5'b00111 : 5'bz;  // Controlled_Buffer controlled_buffer_48
  assign Register_mux = and_21_out ? 2'b10 : 2'bz;  // Controlled_Buffer controlled_buffer_49
  assign ALU_src_B = and_21_out ? 1'b1 : 1'bz;  // Controlled_Buffer controlled_buffer_50
  assign CSR_write_enable = and_21_out ? 1'b0 : 1'bz;  // Controlled_Buffer controlled_buffer_51
  assign CSR_address = and_21_out ? {12{1'b0}} : 12'bz;  // Controlled_Buffer controlled_buffer_52
  assign PC_controll = and_21_out ? 3'b000 : 3'bz;  // Controlled_Buffer controlled_buffer_53
  assign mret = and_21_out ? 1'b0 : 1'bz;  // Controlled_Buffer controlled_buffer_54
  assign kehtiv_opcode = and_21_out ? 1'b1 : 1'bz;  // Controlled_Buffer controlled_buffer_55
  assign Write_enable = and_20_out ? 1'b0 : 1'bz;  // Controlled_Buffer controlled_buffer_56
  assign Data_type = and_20_out ? 3'b000 : 3'bz;  // Controlled_Buffer controlled_buffer_57
  assign ALU_src_A = and_20_out ? 1'b1 : 1'bz;  // Controlled_Buffer controlled_buffer_58
  assign Write_enable = and_21_out ? 1'b0 : 1'bz;  // Controlled_Buffer controlled_buffer_59
  assign Data_type = and_21_out ? 3'b000 : 3'bz;  // Controlled_Buffer controlled_buffer_60
  assign ALU_src_A = and_21_out ? 1'b0 : 1'bz;  // Controlled_Buffer controlled_buffer_61
  and and_22 (and_22_out, Juhis[0], Juhis[1], ~Juhis[2], ~Juhis[3], Juhis[4], ~Juhis[5], ~Juhis[6]);  // AND_Gate
  and and_23 (and_23_out, Juhis[0], Juhis[1], ~Juhis[2], ~Juhis[3], Juhis[4], ~Juhis[5], ~Juhis[6], ~Juhis[12], ~Juhis[13], ~Juhis[14]);  // AND_Gate
  and and_24 (and_24_out, Juhis[0], Juhis[1], ~Juhis[2], ~Juhis[3], Juhis[4], ~Juhis[5], ~Juhis[6], ~Juhis[12], Juhis[13], ~Juhis[14]);  // AND_Gate
  and and_25 (and_25_out, Juhis[0], Juhis[1], ~Juhis[2], ~Juhis[3], Juhis[4], ~Juhis[5], ~Juhis[6], Juhis[12], Juhis[13], ~Juhis[14]);  // AND_Gate
  and and_26 (and_26_out, Juhis[0], Juhis[1], ~Juhis[2], ~Juhis[3], Juhis[4], ~Juhis[5], ~Juhis[6], ~Juhis[12], ~Juhis[13], Juhis[14]);  // AND_Gate
  and and_27 (and_27_out, Juhis[0], Juhis[1], ~Juhis[2], ~Juhis[3], Juhis[4], ~Juhis[5], ~Juhis[6], ~Juhis[12], Juhis[13], Juhis[14]);  // AND_Gate
  and and_28 (and_28_out, Juhis[0], Juhis[1], ~Juhis[2], ~Juhis[3], Juhis[4], ~Juhis[5], ~Juhis[6], ~Juhis[12], Juhis[13], Juhis[14]);  // AND_Gate
  and and_29 (and_29_out, Juhis[0], Juhis[1], ~Juhis[2], ~Juhis[3], Juhis[4], ~Juhis[5], ~Juhis[6], Juhis[12], ~Juhis[13], ~Juhis[14]);  // AND_Gate
  and and_30 (and_30_out, Juhis[0], Juhis[1], ~Juhis[2], ~Juhis[3], Juhis[4], ~Juhis[5], ~Juhis[6], Juhis[12], ~Juhis[13], Juhis[14]);  // AND_Gate
  assign bit_extender_1_out = {{20{Juhis[31]}}, Juhis[31:20]};  // Bit_Extender bit_extender_1
  and and_31 (and_31_out, bit_extender_1_out[31], bit_extender_1_out[30], bit_extender_1_out[29], bit_extender_1_out[28], bit_extender_1_out[27]);
  and and_32 (and_32_out, and_31_out, and_30_out);
  and and_33 (and_33_out, bit_extender_1_out[31], bit_extender_1_out[30], bit_extender_1_out[29], ~bit_extender_1_out[28], bit_extender_1_out[27]);  // AND_Gate
  and and_34 (and_34_out, and_33_out, and_30_out);
  assign rd = and_22_out ? Juhis[11:7] : 5'bz;  // Controlled_Buffer controlled_buffer_62
  assign rs1 = and_22_out ? Juhis[19:15] : 5'bz;  // Controlled_Buffer controlled_buffer_63
  assign rs2 = and_22_out ? {5{1'b0}} : 5'bz;  // Controlled_Buffer controlled_buffer_64
  assign Immidiate = and_22_out ? bit_extender_1_out : 32'bz;  // Controlled_Buffer controlled_buffer_65
  assign ALU_src_A = and_22_out ? 1'b1 : 1'bz;  // Controlled_Buffer controlled_buffer_66
  assign Write_enable = and_22_out ? 1'b0 : 1'bz;  // Controlled_Buffer controlled_buffer_67
  assign Data_type = and_22_out ? 3'b000 : 3'bz;  // Controlled_Buffer controlled_buffer_68
  assign Register_mux = and_22_out ? 2'b10 : 2'bz;  // Controlled_Buffer controlled_buffer_69
  assign CSR_write_enable = and_22_out ? 1'b0 : 1'bz;  // Controlled_Buffer controlled_buffer_70
  assign ALU_src_B = and_22_out ? 1'b1 : 1'bz;  // Controlled_Buffer controlled_buffer_71
  assign CSR_address = and_22_out ? {12{1'b0}} : 12'bz;  // Controlled_Buffer controlled_buffer_72
  assign PC_controll = and_22_out ? 3'b000 : 3'bz;  // Controlled_Buffer controlled_buffer_73
  assign Branch_select = and_22_out ? 1'b0 : 1'bz;  // Controlled_Buffer controlled_buffer_74
  assign mret = and_22_out ? 1'b0 : 1'bz;  // Controlled_Buffer controlled_buffer_75
  assign kehtiv_opcode = and_22_out ? 1'b1 : 1'bz;  // Controlled_Buffer controlled_buffer_76
  assign Command = and_23_out ? {5{1'b0}} : 5'bz;  // Controlled_Buffer controlled_buffer_77
  assign Command = and_24_out ? 5'b10001 : 5'bz;  // Controlled_Buffer controlled_buffer_78
  assign Command = and_25_out ? 5'b00010 : 5'bz;  // Controlled_Buffer controlled_buffer_79
  assign Command = and_26_out ? 5'b01000 : 5'bz;  // Controlled_Buffer controlled_buffer_80
  assign Command = and_27_out ? 5'b00111 : 5'bz;  // Controlled_Buffer controlled_buffer_81
  assign Command = and_28_out ? 5'b00110 : 5'bz;  // Controlled_Buffer controlled_buffer_82
  assign Command = and_29_out ? 5'b00011 : 5'bz;  // Controlled_Buffer controlled_buffer_83
  assign Command = and_32_out ? 5'b00100 : 5'bz;  // Controlled_Buffer controlled_buffer_84
  assign Command = and_34_out ? 5'b00101 : 5'bz;  // Controlled_Buffer controlled_buffer_85
  and and_35 (and_35_out, Juhis[0], Juhis[1], ~Juhis[2], ~Juhis[3], Juhis[4], Juhis[5], Juhis[6]);  // AND_Gate
  or or_1 (or_1_out, Juhis[12], Juhis[13], Juhis[14]);
  and and_36 (and_36_out, Juhis[0], Juhis[1], ~Juhis[2], ~Juhis[3], Juhis[4], Juhis[5], Juhis[6], Juhis[12], ~Juhis[13], ~Juhis[14]);  // AND_Gate
  and and_37 (and_37_out, Juhis[0], Juhis[1], ~Juhis[2], ~Juhis[3], Juhis[4], Juhis[5], Juhis[6], ~Juhis[12], Juhis[13], ~Juhis[14]);  // AND_Gate
  and and_38 (and_38_out, Juhis[0], Juhis[1], ~Juhis[2], ~Juhis[3], Juhis[4], Juhis[5], Juhis[6], Juhis[12], Juhis[13], ~Juhis[14]);  // AND_Gate
  and and_39 (and_39_out, Juhis[0], Juhis[1], ~Juhis[2], ~Juhis[3], Juhis[4], Juhis[5], Juhis[6], Juhis[12], ~Juhis[13], Juhis[14]);  // AND_Gate
  and and_40 (and_40_out, Juhis[0], Juhis[1], ~Juhis[2], ~Juhis[3], Juhis[4], Juhis[5], Juhis[6], ~Juhis[12], Juhis[13], Juhis[14]);  // AND_Gate
  and and_41 (and_41_out, Juhis[0], Juhis[1], ~Juhis[2], ~Juhis[3], Juhis[4], Juhis[5], Juhis[6], Juhis[12], Juhis[13], Juhis[14]);  // AND_Gate
  and and_42 (and_42_out, and_35_out, or_1_out);
  assign bit_extender_2_out = {{27{1'b0}}, Juhis[24:20]};  // Bit_Extender bit_extender_2
  assign rd = and_42_out ? Juhis[11:7] : 5'bz;  // Controlled_Buffer controlled_buffer_86
  assign rs1 = and_42_out ? Juhis[19:15] : 5'bz;  // Controlled_Buffer controlled_buffer_87
  assign rs2 = and_42_out ? {5{1'b0}} : 5'bz;  // Controlled_Buffer controlled_buffer_88
  assign CSR_address = and_42_out ? Juhis[31:20] : 12'bz;  // Controlled_Buffer controlled_buffer_89
  assign Immidiate = and_42_out ? bit_extender_2_out : 32'bz;  // Controlled_Buffer controlled_buffer_90
  assign ALU_src_A = and_42_out ? 1'b1 : 1'bz;  // Controlled_Buffer controlled_buffer_91
  assign CSR_write_enable = and_42_out ? 1'b1 : 1'bz;  // Controlled_Buffer controlled_buffer_92
  assign Write_enable = and_42_out ? 1'b0 : 1'bz;  // Controlled_Buffer controlled_buffer_93
  assign Data_type = and_42_out ? 3'b000 : 3'bz;  // Controlled_Buffer controlled_buffer_94
  assign Register_mux = and_42_out ? 2'b01 : 2'bz;  // Controlled_Buffer controlled_buffer_95
  assign PC_controll = and_42_out ? 3'b000 : 3'bz;  // Controlled_Buffer controlled_buffer_96
  assign mret = and_42_out ? 1'b0 : 1'bz;  // Controlled_Buffer controlled_buffer_97
  assign kehtiv_opcode = and_42_out ? 1'b1 : 1'bz;  // Controlled_Buffer controlled_buffer_98
  assign Command = and_36_out ? {5{1'b0}} : 5'bz;  // Controlled_Buffer controlled_buffer_99
  assign ALU_src_B = and_36_out ? 1'b0 : 1'bz;  // Controlled_Buffer controlled_buffer_100
  assign Command = and_37_out ? 5'b00111 : 5'bz;  // Controlled_Buffer controlled_buffer_101
  assign ALU_src_B = and_37_out ? 1'b0 : 1'bz;  // Controlled_Buffer controlled_buffer_102
  assign Command = and_38_out ? 5'b01000 : 5'bz;  // Controlled_Buffer controlled_buffer_103
  assign ALU_src_B = and_38_out ? 1'b0 : 1'bz;  // Controlled_Buffer controlled_buffer_104
  assign Command = and_39_out ? {5{1'b0}} : 5'bz;  // Controlled_Buffer controlled_buffer_105
  assign ALU_src_B = and_39_out ? 1'b1 : 1'bz;  // Controlled_Buffer controlled_buffer_106
  assign Command = and_40_out ? 5'b00111 : 5'bz;  // Controlled_Buffer controlled_buffer_107
  assign ALU_src_B = and_40_out ? 1'b1 : 1'bz;  // Controlled_Buffer controlled_buffer_108
  assign Command = and_41_out ? 5'b01000 : 5'bz;  // Controlled_Buffer controlled_buffer_109
  assign ALU_src_B = and_41_out ? 1'b1 : 1'bz;  // Controlled_Buffer controlled_buffer_110
  assign bit_extender_3_out = {{11{Juhis[31]}}, Juhis[31]};  // Bit_Extender bit_extender_3
  and and_43 (and_43_out, Juhis[0], Juhis[1], Juhis[2], Juhis[3], ~Juhis[4], Juhis[5], Juhis[6]);  // AND_Gate
  and and_44 (and_44_out, Juhis[0], Juhis[1], Juhis[2], ~Juhis[3], ~Juhis[4], Juhis[5], Juhis[6], ~Juhis[12], ~Juhis[13], ~Juhis[14]);  // AND_Gate
  assign bit_extender_4_out = {{20{Juhis[31]}}, Juhis[31:20]};  // Bit_Extender bit_extender_4
  assign Immidiate = and_43_out ? {bit_extender_3_out, Juhis[19:12], Juhis[20], Juhis[30:21], 1'b0} : 32'bz;  // Controlled_Buffer controlled_buffer_111
  assign Command = and_43_out ? {5{1'b0}} : 5'bz;  // Controlled_Buffer controlled_buffer_112
  assign Register_mux = and_43_out ? 2'b00 : 2'bz;  // Controlled_Buffer controlled_buffer_113
  assign ALU_src_A = and_43_out ? 1'b0 : 1'bz;  // Controlled_Buffer controlled_buffer_114
  assign rs1 = and_43_out ? {5{1'b0}} : 5'bz;  // Controlled_Buffer controlled_buffer_115
  assign rs2 = and_43_out ? {5{1'b0}} : 5'bz;  // Controlled_Buffer controlled_buffer_116
  assign rd = and_43_out ? Juhis[11:7] : 5'bz;  // Controlled_Buffer controlled_buffer_117
  assign Data_type = and_43_out ? 3'b000 : 3'bz;  // Controlled_Buffer controlled_buffer_118
  assign ALU_src_B = and_43_out ? 1'b1 : 1'bz;  // Controlled_Buffer controlled_buffer_119
  assign Write_enable = and_43_out ? 1'b0 : 1'bz;  // Controlled_Buffer controlled_buffer_120
  assign CSR_write_enable = and_43_out ? 1'b0 : 1'bz;  // Controlled_Buffer controlled_buffer_121
  assign CSR_address = and_43_out ? {12{1'b0}} : 12'bz;  // Controlled_Buffer controlled_buffer_122
  assign PC_controll = and_43_out ? 3'b001 : 3'bz;  // Controlled_Buffer controlled_buffer_123
  assign mret = and_43_out ? 1'b0 : 1'bz;  // Controlled_Buffer controlled_buffer_124
  assign kehtiv_opcode = and_43_out ? 1'b1 : 1'bz;  // Controlled_Buffer controlled_buffer_125
  assign Immidiate = and_44_out ? bit_extender_4_out : 32'bz;  // Controlled_Buffer controlled_buffer_126
  assign Command = and_44_out ? {5{1'b0}} : 5'bz;  // Controlled_Buffer controlled_buffer_127
  assign Register_mux = and_44_out ? 2'b00 : 2'bz;  // Controlled_Buffer controlled_buffer_128
  assign ALU_src_A = and_44_out ? 1'b1 : 1'bz;  // Controlled_Buffer controlled_buffer_129
  assign rs1 = and_44_out ? Juhis[19:15] : 5'bz;  // Controlled_Buffer controlled_buffer_130
  assign rs2 = and_44_out ? {5{1'b0}} : 5'bz;  // Controlled_Buffer controlled_buffer_131
  assign rd = and_44_out ? Juhis[11:7] : 5'bz;  // Controlled_Buffer controlled_buffer_132
  assign Data_type = and_44_out ? 3'b000 : 3'bz;  // Controlled_Buffer controlled_buffer_133
  assign ALU_src_B = and_44_out ? 1'b1 : 1'bz;  // Controlled_Buffer controlled_buffer_134
  assign Write_enable = and_44_out ? 1'b0 : 1'bz;  // Controlled_Buffer controlled_buffer_135
  assign CSR_write_enable = and_44_out ? 1'b0 : 1'bz;  // Controlled_Buffer controlled_buffer_136
  assign CSR_address = and_44_out ? {12{1'b0}} : 12'bz;  // Controlled_Buffer controlled_buffer_137
  assign PC_controll = and_44_out ? 3'b001 : 3'bz;  // Controlled_Buffer controlled_buffer_138
  assign mret = and_44_out ? 1'b0 : 1'bz;  // Controlled_Buffer controlled_buffer_139
  assign kehtiv_opcode = and_44_out ? 1'b1 : 1'bz;  // Controlled_Buffer controlled_buffer_140
  and and_45 (and_45_out, Juhis[0], Juhis[1], ~Juhis[2], ~Juhis[3], ~Juhis[4], Juhis[5], Juhis[6]);  // AND_Gate
  assign bit_extender_5_out = {{19{Juhis[31]}}, {Juhis[31], Juhis[7], Juhis[30:25], Juhis[11:8], 1'b0}};  // Bit_Extender bit_extender_5
  and and_46 (and_46_out, and_45_out, ~Juhis[12], ~Juhis[13], ~Juhis[14]);  // AND_Gate
  and and_47 (and_47_out, and_45_out, Juhis[12], ~Juhis[13], ~Juhis[14]);  // AND_Gate
  and and_48 (and_48_out, and_45_out, ~Juhis[12], ~Juhis[13], Juhis[14]);  // AND_Gate
  and and_49 (and_49_out, and_45_out, Juhis[12], ~Juhis[13], Juhis[14]);  // AND_Gate
  and and_50 (and_50_out, and_45_out, ~Juhis[12], Juhis[13], Juhis[14]);  // AND_Gate
  and and_51 (and_51_out, and_45_out, Juhis[12], Juhis[13], Juhis[14]);
  assign Immidiate = and_45_out ? bit_extender_5_out : 32'bz;  // Controlled_Buffer controlled_buffer_141
  assign Register_mux = and_45_out ? 2'b00 : 2'bz;  // Controlled_Buffer controlled_buffer_142
  assign ALU_src_A = and_45_out ? 1'b1 : 1'bz;  // Controlled_Buffer controlled_buffer_143
  assign rs1 = and_45_out ? Juhis[19:15] : 5'bz;  // Controlled_Buffer controlled_buffer_144
  assign rs2 = and_45_out ? Juhis[24:20] : 5'bz;  // Controlled_Buffer controlled_buffer_145
  assign rd = and_45_out ? {5{1'b0}} : 5'bz;  // Controlled_Buffer controlled_buffer_146
  assign Data_type = and_45_out ? 3'b000 : 3'bz;  // Controlled_Buffer controlled_buffer_147
  assign ALU_src_B = and_45_out ? 1'b0 : 1'bz;  // Controlled_Buffer controlled_buffer_148
  assign Write_enable = and_45_out ? 1'b0 : 1'bz;  // Controlled_Buffer controlled_buffer_149
  assign CSR_write_enable = and_45_out ? 1'b0 : 1'bz;  // Controlled_Buffer controlled_buffer_150
  assign CSR_address = and_45_out ? {12{1'b0}} : 12'bz;  // Controlled_Buffer controlled_buffer_151
  assign PC_controll = and_45_out ? 3'b100 : 3'bz;  // Controlled_Buffer controlled_buffer_152
  assign mret = and_45_out ? 1'b0 : 1'bz;  // Controlled_Buffer controlled_buffer_153
  assign kehtiv_opcode = and_45_out ? 1'b1 : 1'bz;  // Controlled_Buffer controlled_buffer_154
  assign Branch_select = and_46_out ? 1'b1 : 1'bz;  // Controlled_Buffer controlled_buffer_155
  assign Command = and_46_out ? 5'b01001 : 5'bz;  // Controlled_Buffer controlled_buffer_156
  assign Branch_select = and_47_out ? 1'b0 : 1'bz;  // Controlled_Buffer controlled_buffer_157
  assign Command = and_47_out ? 5'b01001 : 5'bz;  // Controlled_Buffer controlled_buffer_158
  assign Branch_select = and_48_out ? 1'b0 : 1'bz;  // Controlled_Buffer controlled_buffer_159
  assign Command = and_48_out ? 5'b01001 : 5'bz;  // Controlled_Buffer controlled_buffer_160
  assign Branch_select = and_49_out ? 1'b1 : 1'bz;  // Controlled_Buffer controlled_buffer_161
  assign Command = and_49_out ? 5'b01001 : 5'bz;  // Controlled_Buffer controlled_buffer_162
  assign Branch_select = and_50_out ? 1'b0 : 1'bz;  // Controlled_Buffer controlled_buffer_163
  assign Command = and_50_out ? 5'b00010 : 5'bz;  // Controlled_Buffer controlled_buffer_164
  assign Branch_select = and_51_out ? 1'b1 : 1'bz;  // Controlled_Buffer controlled_buffer_165
  assign Command = and_51_out ? 5'b00010 : 5'bz;  // Controlled_Buffer controlled_buffer_166
  and and_52 (and_52_out, Juhis[0], Juhis[1], ~Juhis[2], ~Juhis[3], Juhis[4], Juhis[5], Juhis[6], ~Juhis[7], ~Juhis[8], ~Juhis[9], ~Juhis[10], ~Juhis[11], ~Juhis[12], ~Juhis[13], ~Juhis[14], ~Juhis[15], ~Juhis[17], ~Juhis[18], ~Juhis[19], Juhis[20], ~Juhis[21], Juhis[22], ~Juhis[23], ~Juhis[24], ~Juhis[25], ~Juhis[26], ~Juhis[27], Juhis[28], ~Juhis[29], ~Juhis[30], ~Juhis[31], ~Juhis[16]);  // AND_Gate
  and and_53 (and_53_out, Juhis[0], Juhis[1], ~Juhis[2], ~Juhis[3], Juhis[4], Juhis[5], Juhis[6], ~Juhis[7], ~Juhis[8], ~Juhis[9], ~Juhis[10], ~Juhis[11], ~Juhis[12], ~Juhis[13], ~Juhis[14], ~Juhis[15], ~Juhis[17], ~Juhis[18], ~Juhis[19], ~Juhis[20], ~Juhis[21], ~Juhis[22], ~Juhis[23], ~Juhis[24], ~Juhis[25], ~Juhis[26], ~Juhis[27], ~Juhis[28], ~Juhis[29], ~Juhis[30], ~Juhis[31], ~Juhis[16]);  // AND_Gate
  and and_54 (and_54_out, Juhis[0], Juhis[1], ~Juhis[2], ~Juhis[3], Juhis[4], Juhis[5], Juhis[6], ~Juhis[7], ~Juhis[8], ~Juhis[9], ~Juhis[10], ~Juhis[11], ~Juhis[12], ~Juhis[13], ~Juhis[14], ~Juhis[15], ~Juhis[17], ~Juhis[18], ~Juhis[19], Juhis[20], ~Juhis[21], ~Juhis[22], ~Juhis[23], ~Juhis[24], ~Juhis[25], ~Juhis[26], ~Juhis[27], ~Juhis[28], ~Juhis[29], ~Juhis[30], ~Juhis[31], ~Juhis[16]);  // AND_Gate
  assign kehtiv_opcode = and_52_out ? 1'b1 : 1'bz;  // Controlled_Buffer controlled_buffer_167
  assign Immidiate = and_52_out ? {32{1'b0}} : 32'bz;  // Controlled_Buffer controlled_buffer_168
  assign Register_mux = and_52_out ? 2'b00 : 2'bz;  // Controlled_Buffer controlled_buffer_169
  assign ALU_src_A = and_52_out ? 1'b0 : 1'bz;  // Controlled_Buffer controlled_buffer_170
  assign rs1 = and_52_out ? {5{1'b0}} : 5'bz;  // Controlled_Buffer controlled_buffer_171
  assign rs2 = and_52_out ? {5{1'b0}} : 5'bz;  // Controlled_Buffer controlled_buffer_172
  assign rd = and_52_out ? {5{1'b0}} : 5'bz;  // Controlled_Buffer controlled_buffer_173
  assign Data_type = and_52_out ? 3'b000 : 3'bz;  // Controlled_Buffer controlled_buffer_174
  assign ALU_src_B = and_52_out ? 1'b1 : 1'bz;  // Controlled_Buffer controlled_buffer_175
  assign Write_enable = and_52_out ? 1'b0 : 1'bz;  // Controlled_Buffer controlled_buffer_176
  assign CSR_write_enable = and_52_out ? 1'b0 : 1'bz;  // Controlled_Buffer controlled_buffer_177
  assign CSR_address = and_52_out ? {12{1'b0}} : 12'bz;  // Controlled_Buffer controlled_buffer_178
  assign PC_controll = and_52_out ? 3'b010 : 3'bz;  // Controlled_Buffer controlled_buffer_179
  assign Branch_select = and_52_out ? 1'b0 : 1'bz;  // Controlled_Buffer controlled_buffer_180
  assign Command = and_52_out ? 5'b01001 : 5'bz;  // Controlled_Buffer controlled_buffer_181
  assign kehtiv_opcode = and_53_out ? 1'b1 : 1'bz;  // Controlled_Buffer controlled_buffer_182
  assign Immidiate = and_53_out ? {32{1'b0}} : 32'bz;  // Controlled_Buffer controlled_buffer_183
  assign Register_mux = and_53_out ? 2'b00 : 2'bz;  // Controlled_Buffer controlled_buffer_184
  assign ALU_src_A = and_53_out ? 1'b0 : 1'bz;  // Controlled_Buffer controlled_buffer_185
  assign rs1 = and_53_out ? {5{1'b0}} : 5'bz;  // Controlled_Buffer controlled_buffer_186
  assign rs2 = and_53_out ? {5{1'b0}} : 5'bz;  // Controlled_Buffer controlled_buffer_187
  assign rd = and_53_out ? {5{1'b0}} : 5'bz;  // Controlled_Buffer controlled_buffer_188
  assign Data_type = and_53_out ? 3'b000 : 3'bz;  // Controlled_Buffer controlled_buffer_189
  assign ALU_src_B = and_53_out ? 1'b1 : 1'bz;  // Controlled_Buffer controlled_buffer_190
  assign Write_enable = and_53_out ? 1'b0 : 1'bz;  // Controlled_Buffer controlled_buffer_191
  assign CSR_write_enable = and_53_out ? 1'b0 : 1'bz;  // Controlled_Buffer controlled_buffer_192
  assign CSR_address = and_53_out ? {12{1'b0}} : 12'bz;  // Controlled_Buffer controlled_buffer_193
  assign PC_controll = and_53_out ? 3'b010 : 3'bz;  // Controlled_Buffer controlled_buffer_194
  assign Branch_select = and_53_out ? 1'b0 : 1'bz;  // Controlled_Buffer controlled_buffer_195
  assign Command = and_53_out ? 5'b01001 : 5'bz;  // Controlled_Buffer controlled_buffer_196
  assign mret = and_53_out ? 1'b1 : 1'bz;  // Controlled_Buffer controlled_buffer_197
  assign Immidiate = and_54_out ? {32{1'b0}} : 32'bz;  // Controlled_Buffer controlled_buffer_198
  assign Register_mux = and_54_out ? 2'b00 : 2'bz;  // Controlled_Buffer controlled_buffer_199
  assign ALU_src_A = and_54_out ? 1'b0 : 1'bz;  // Controlled_Buffer controlled_buffer_200
  assign rs1 = and_54_out ? {5{1'b0}} : 5'bz;  // Controlled_Buffer controlled_buffer_201
  assign rs2 = and_54_out ? {5{1'b0}} : 5'bz;  // Controlled_Buffer controlled_buffer_202
  assign rd = and_54_out ? {5{1'b0}} : 5'bz;  // Controlled_Buffer controlled_buffer_203
  assign Data_type = and_54_out ? 3'b000 : 3'bz;  // Controlled_Buffer controlled_buffer_204
  assign ALU_src_B = and_54_out ? 1'b1 : 1'bz;  // Controlled_Buffer controlled_buffer_205
  assign Write_enable = and_54_out ? 1'b0 : 1'bz;  // Controlled_Buffer controlled_buffer_206
  assign CSR_write_enable = and_54_out ? 1'b0 : 1'bz;  // Controlled_Buffer controlled_buffer_207
  assign CSR_address = and_54_out ? {12{1'b0}} : 12'bz;  // Controlled_Buffer controlled_buffer_208
  assign PC_controll = and_54_out ? 3'b010 : 3'bz;  // Controlled_Buffer controlled_buffer_209
  assign Branch_select = and_54_out ? 1'b0 : 1'bz;  // Controlled_Buffer controlled_buffer_210
  assign Command = and_54_out ? 5'b01001 : 5'bz;  // Controlled_Buffer controlled_buffer_211
  assign mret = and_54_out ? 1'b0 : 1'bz;  // Controlled_Buffer controlled_buffer_212
  assign kehtiv_opcode = and_54_out ? 1'b1 : 1'bz;  // Controlled_Buffer controlled_buffer_213
  assign bit_extender_6_out = {{20{Juhis[31]}}, {Juhis[31:25], Juhis[11:7]}};  // Bit_Extender bit_extender_6
  and and_55 (and_55_out, Juhis[0], Juhis[1], ~Juhis[2], ~Juhis[3], ~Juhis[4], Juhis[5], ~Juhis[6]);  // AND_Gate
  and and_56 (and_56_out, and_55_out, ~Juhis[12], ~Juhis[13], ~Juhis[14]);  // AND_Gate
  and and_57 (and_57_out, and_55_out, Juhis[12], ~Juhis[13], ~Juhis[14]);  // AND_Gate
  and and_58 (and_58_out, and_55_out, ~Juhis[12], Juhis[13], ~Juhis[14]);  // AND_Gate
  assign Immidiate = and_55_out ? bit_extender_6_out : 32'bz;  // Controlled_Buffer controlled_buffer_214
  assign Register_mux = and_55_out ? 2'b00 : 2'bz;  // Controlled_Buffer controlled_buffer_215
  assign ALU_src_A = and_55_out ? 1'b1 : 1'bz;  // Controlled_Buffer controlled_buffer_216
  assign rs1 = and_55_out ? Juhis[19:15] : 5'bz;  // Controlled_Buffer controlled_buffer_217
  assign rs2 = and_55_out ? Juhis[24:20] : 5'bz;  // Controlled_Buffer controlled_buffer_218
  assign rd = and_55_out ? {5{1'b0}} : 5'bz;  // Controlled_Buffer controlled_buffer_219
  assign Command = and_55_out ? {5{1'b0}} : 5'bz;  // Controlled_Buffer controlled_buffer_220
  assign ALU_src_B = and_55_out ? 1'b1 : 1'bz;  // Controlled_Buffer controlled_buffer_221
  assign Write_enable = and_55_out ? 1'b1 : 1'bz;  // Controlled_Buffer controlled_buffer_222
  assign CSR_write_enable = and_55_out ? 1'b0 : 1'bz;  // Controlled_Buffer controlled_buffer_223
  assign CSR_address = and_55_out ? {12{1'b0}} : 12'bz;  // Controlled_Buffer controlled_buffer_224
  assign PC_controll = and_55_out ? 3'b000 : 3'bz;  // Controlled_Buffer controlled_buffer_225
  assign Branch_select = and_55_out ? 1'b0 : 1'bz;  // Controlled_Buffer controlled_buffer_226
  assign mret = and_55_out ? 1'b0 : 1'bz;  // Controlled_Buffer controlled_buffer_227
  assign kehtiv_opcode = and_55_out ? 1'b1 : 1'bz;  // Controlled_Buffer controlled_buffer_228
  assign Data_type = and_56_out ? 3'b111 : 3'bz;  // Controlled_Buffer controlled_buffer_229
  assign Data_type = and_57_out ? 3'b110 : 3'bz;  // Controlled_Buffer controlled_buffer_230
  assign Data_type = and_58_out ? 3'b101 : 3'bz;  // Controlled_Buffer controlled_buffer_231
  assign bit_extender_7_out = {{20{Juhis[31]}}, Juhis[31:20]};  // Bit_Extender bit_extender_7
  and and_59 (and_59_out, Juhis[0], Juhis[1], ~Juhis[2], ~Juhis[3], ~Juhis[4], ~Juhis[5], ~Juhis[6]);  // AND_Gate
  assign kehtiv_opcode = and_59_out ? 1'b1 : 1'bz;  // Controlled_Buffer controlled_buffer_232
  and and_60 (and_60_out, and_59_out, ~Juhis[12], ~Juhis[13], ~Juhis[14]);  // AND_Gate
  and and_61 (and_61_out, and_59_out, Juhis[12], ~Juhis[13], ~Juhis[14]);  // AND_Gate
  and and_62 (and_62_out, and_59_out, ~Juhis[12], Juhis[13], ~Juhis[14]);  // AND_Gate
  and and_63 (and_63_out, and_59_out, ~Juhis[12], ~Juhis[13], Juhis[14]);  // AND_Gate
  and and_64 (and_64_out, and_59_out, Juhis[12], ~Juhis[13], Juhis[14]);  // AND_Gate
  assign Immidiate = and_59_out ? bit_extender_7_out : 32'bz;  // Controlled_Buffer controlled_buffer_233
  assign Register_mux = and_59_out ? 2'b11 : 2'bz;  // Controlled_Buffer controlled_buffer_234
  assign ALU_src_A = and_59_out ? 1'b1 : 1'bz;  // Controlled_Buffer controlled_buffer_235
  assign rs1 = and_59_out ? Juhis[19:15] : 5'bz;  // Controlled_Buffer controlled_buffer_236
  assign rs2 = and_59_out ? {5{1'b0}} : 5'bz;  // Controlled_Buffer controlled_buffer_237
  assign rd = and_59_out ? Juhis[11:7] : 5'bz;  // Controlled_Buffer controlled_buffer_238
  assign Command = and_59_out ? {5{1'b0}} : 5'bz;  // Controlled_Buffer controlled_buffer_239
  assign ALU_src_B = and_59_out ? 1'b1 : 1'bz;  // Controlled_Buffer controlled_buffer_240
  assign Write_enable = and_59_out ? 1'b0 : 1'bz;  // Controlled_Buffer controlled_buffer_241
  assign CSR_write_enable = and_59_out ? 1'b0 : 1'bz;  // Controlled_Buffer controlled_buffer_242
  assign CSR_address = and_59_out ? {12{1'b0}} : 12'bz;  // Controlled_Buffer controlled_buffer_243
  assign PC_controll = and_59_out ? 3'b000 : 3'bz;  // Controlled_Buffer controlled_buffer_244
  assign Branch_select = and_59_out ? 1'b1 : 1'bz;  // Controlled_Buffer controlled_buffer_245
  assign mret = and_59_out ? 1'b0 : 1'bz;  // Controlled_Buffer controlled_buffer_246
  assign Data_type = and_60_out ? 3'b011 : 3'bz;  // Controlled_Buffer controlled_buffer_247
  assign Data_type = and_61_out ? 3'b001 : 3'bz;  // Controlled_Buffer controlled_buffer_248
  assign Data_type = and_62_out ? 3'b000 : 3'bz;  // Controlled_Buffer controlled_buffer_249
  assign Data_type = and_63_out ? 3'b100 : 3'bz;  // Controlled_Buffer controlled_buffer_250
  assign Data_type = and_64_out ? 3'b010 : 3'bz;  // Controlled_Buffer controlled_buffer_251

  // Other names for the same wires on the sheet: kehtiv = kehtiv_opcode; PC_ctrl[2:0] = PC_controll

  // Notes on the sheet:
  //   Juhis: initial=0x1
  //   mret: pull=down
  //   kehtiv_opcode: pull=down
  //   ADD
  //   SUB
  //   AND
  //   OR
  //   XOR
  //   SLL
  //   SLT
  //   SLT
  //   SRL
  //   SRA
  //   MUL
  //   MULH
  //   MULHU
  //   MULHSU
  //   DIVU
  //   REMU
  //   DIV
  //   REM
  //   R type
  //   LUI
  //   AUIPC
  //   U type
  //   ADDI
  //   SLTI
  //   SLTIU
  //   XORI
  //   ORI
  //   ANDI
  //   SLLI
  //   SRLI
  //   SRAI
  //   I type
  //   I type CSR
  //   CSRRW
  //   CSRRS
  //   CSRRC
  //   CSRRWI
  //   CSRRSI
  //   CSRRCI
  //   JAL
  //   JALR
  //   Jumps
  //   BEQ
  //   BNE
  //   BLT
  //   BGE
  //   BLTU
  //   BGEU
  //   B type (branch)
  //   WFI
  //   ECALL
  //   EBREAK
  //   Store
  //   SB
  //   SH
  //   SW
  //   Malu kasud
  //   Load
  //   LB
  //   LH
  //   LW
  //   LBU
  //   LHU
endmodule

module Microcontroller (
  input  PCLK,
  input  ADDR,
  input  BOOT,
  input  DATA
);

  wire aadressi_vordleja_1_output_1, aadressi_vordleja_2_output_1, and_1_out, and_2_out, and_3_out,
       and_4_out, and_5_out, and_6_out, clock_1_out, counter_1_carry, CPU_1_kirjuta_mallu, nor_1_out,
       not_1_out, not_2_out, or_1_out, or_2_out, reset_out;
  wire [1:0] and_7_out, and_8_out, or_3_out, PA_p3_2, Timer_adv_1_viigu_kontroll, Timer_adv_1_viigud_valja,
       undriven;
  wire [19:0] Timer_adv_1_erandid;
  wire [29:0] counter_2_q;
  wire [30:0] shift_register_1_out;
  wire [31:0] and_9_out, and_10_out, controlled_buffer_1_out, CPU_1_alu_valjund, CPU_1_juhise_aadress,
       CPU_1_malu_valjund, multiplexer_1_out, or_4_out, PA_p3, ram_1_dout, RAM_1_dout_2, register_1_q,
       register_2_q;

  Button reset (.out(reset_out));
  Clock clock_1 (.out(clock_1_out));
  or or_1 (or_1_out, PCLK, clock_1_out);
  Shift_Register #(.length(31)) shift_register_1 (
    .shift(1'b1), .in(DATA), .clk(or_1_out), .out(shift_register_1_out[0]), .q0(shift_register_1_out[30]),
    .q1(shift_register_1_out[29]), .q2(shift_register_1_out[28]), .q3(shift_register_1_out[27]),
    .q4(shift_register_1_out[26]), .q5(shift_register_1_out[25]), .q6(shift_register_1_out[24]),
    .q7(shift_register_1_out[23]), .q8(shift_register_1_out[22]), .q9(shift_register_1_out[21]),
    .q10(shift_register_1_out[20]), .q11(shift_register_1_out[19]), .q12(shift_register_1_out[18]),
    .q13(shift_register_1_out[17]), .q14(shift_register_1_out[16]), .q15(shift_register_1_out[15]),
    .q16(shift_register_1_out[14]), .q17(shift_register_1_out[13]), .q18(shift_register_1_out[12]),
    .q19(shift_register_1_out[11]), .q20(shift_register_1_out[10]), .q21(shift_register_1_out[9]),
    .q22(shift_register_1_out[8]), .q23(shift_register_1_out[7]), .q24(shift_register_1_out[6]),
    .q25(shift_register_1_out[5]), .q26(shift_register_1_out[4]), .q27(shift_register_1_out[3]),
    .q28(shift_register_1_out[2]), .q29(shift_register_1_out[1]));  // open: load, clr, d0, d1, d2, d3, d4, d5, d6, d7, d8, d9, d10, d11, d12, d13, d14, d15, d16, d17, d18, d19, d20, d21, d22, d23, d24, d25, d26, d27, d28, d29, d30, q30
  Counter #(.max('h1f), .width(5)) counter_1 (
    .carry(counter_1_carry), .clk(or_1_out), .clr(not_1_out));  // open: load, D, count, Q, up
  not not_1 (not_1_out, BOOT);
  and and_1 (and_1_out, or_1_out, ~BOOT);  // AND_Gate
  ROM #(.addrWidth(16), .dataWidth(32)) ROM_1 ();  // open: addr, data
  not not_2 (not_2_out, BOOT);
  Counter #(.max('h3fffffff), .width(30)) counter_2 (
    .load(ADDR), .D({DATA, shift_register_1_out[30:2]}), .Q(counter_2_q), .clk(counter_1_carry),
    .clr(not_2_out));  // open: count, carry, up
  and and_2 (and_2_out, counter_1_carry, ~ADDR);  // AND_Gate
  Multiplexer #(.width(32)) multiplexer_1 (
    .in0(CPU_1_juhise_aadress), .in1({counter_2_q, undriven}), .out(multiplexer_1_out), .sel(BOOT));
  or or_2 (or_2_out, multiplexer_1_out[30], multiplexer_1_out[31], multiplexer_1_out[29], multiplexer_1_out[28]);
  and and_3 (and_3_out, ~or_2_out, and_2_out);  // AND_Gate
  // Probe on multiplexer_1_out[17:2]
  RAM #(.addrWidth(16), .dataWidth(32), .enables("line")) ram_1 (
    .addr(multiplexer_1_out[17:2]), .we(and_3_out), .clk(and_3_out), .din({DATA, shift_register_1_out}),
    .dout(ram_1_dout));
  CPU CPU_1 (
    .juhis(ram_1_dout), .malu_sisend(controlled_buffer_1_out), .reset(reset_out), .clk(and_1_out),
    .Ext_Interrupt(Timer_adv_1_erandid), .juhise_aadress(CPU_1_juhise_aadress),
    .ALU_valjund(CPU_1_alu_valjund), .kirjuta_mallu(CPU_1_kirjuta_mallu), .malu_valjund(CPU_1_malu_valjund));
  and and_4 (and_4_out, CPU_1_kirjuta_mallu, nor_1_out);
  nor nor_1 (nor_1_out, ~CPU_1_alu_valjund[14], CPU_1_alu_valjund[15], CPU_1_alu_valjund[16], CPU_1_alu_valjund[17], CPU_1_alu_valjund[18], CPU_1_alu_valjund[19], CPU_1_alu_valjund[20], CPU_1_alu_valjund[21], CPU_1_alu_valjund[22], CPU_1_alu_valjund[24], CPU_1_alu_valjund[25], CPU_1_alu_valjund[26], CPU_1_alu_valjund[27], CPU_1_alu_valjund[28], CPU_1_alu_valjund[29], CPU_1_alu_valjund[30], CPU_1_alu_valjund[31], CPU_1_alu_valjund[23]);  // NOR_Gate
  // Probe on CPU_1_alu_valjund[13:2]
  RAM #(.addrWidth(12), .dataWidth(32), .enables("line")) RAM_1_dup2 (
    .addr(CPU_1_alu_valjund[13:2]), .we(and_4_out), .clk(and_1_out), .din(CPU_1_malu_valjund),
    .dout(RAM_1_dout_2));
  assign controlled_buffer_1_out = nor_1_out ? RAM_1_dout_2 : 32'bz;  // Controlled_Buffer controlled_buffer_1
  // Probe on CPU_1_alu_valjund
  aadressi_vordleja aadressi_vordleja_1 (
    .Input_bus_1(CPU_1_alu_valjund), .Input_bus_2({32{1'b0}}), .Output_1(aadressi_vordleja_1_output_1));
  aadressi_vordleja aadressi_vordleja_2 (
    .Input_bus_1(CPU_1_alu_valjund), .Input_bus_2(32'h4), .Output_1(aadressi_vordleja_2_output_1));
  // Probe on CPU_1_alu_valjund
  Register #(.width(32)) register_1 (
    .D(CPU_1_malu_valjund), .en(and_5_out), .clk(and_1_out), .Q(register_1_q));  // open: clr
  and and_5 (and_5_out, CPU_1_kirjuta_mallu, aadressi_vordleja_1_output_1);
  Register #(.width(32)) register_2 (
    .D(CPU_1_malu_valjund), .en(and_6_out), .clk(and_1_out), .Q(register_2_q));  // open: clr
  and and_6 (and_6_out, CPU_1_kirjuta_mallu, aadressi_vordleja_2_output_1);
  assign controlled_buffer_1_out = aadressi_vordleja_2_output_1 ? register_2_q : 32'bz;  // Controlled_Buffer controlled_buffer_2
  Timer_adv Timer_adv_1 (
    .Andmed_sisse(CPU_1_malu_valjund), .Malu_aadress(CPU_1_alu_valjund), .TMR_ADDR(32'h100),
    .Luba_kirjutamine(CPU_1_kirjuta_mallu), .Viigud_sisse(PA_p3_2), .CLK(and_1_out),
    .Andmed_valja(controlled_buffer_1_out), .Erandid(Timer_adv_1_erandid[3:0]),
    .Viigud_valja(Timer_adv_1_viigud_valja), .Viigu_kontroll(Timer_adv_1_viigu_kontroll));
  assign and_7_out = ~Timer_adv_1_viigu_kontroll & register_1_q[26:25];  // AND_Gate and_7, 2 bits wide
  // Probe on Timer_adv_1_viigud_valja
  assign and_8_out = Timer_adv_1_viigu_kontroll & Timer_adv_1_viigud_valja;  // AND_Gate and_8, 2 bits wide
  assign or_3_out = and_8_out | and_7_out;  // OR_Gate or_3, 2 bits wide
  assign controlled_buffer_1_out = aadressi_vordleja_1_output_1 ? or_4_out : 32'bz;  // Controlled_Buffer controlled_buffer_3
  assign or_4_out = and_9_out | and_10_out;  // OR_Gate or_4, 32 bits wide
  assign and_9_out = register_2_q & {register_1_q[31:27], or_3_out, register_1_q[24:0]};  // AND_Gate and_9, 32 bits wide
  // PortIO #(.direction("IOMultiEnable"), .number(32)) PA: pin names not known; wires that end beside it: register_2_q, {register_1_q[31:27], or_3_out, register_1_q[24:0]}, {PA_p3[31:9], PA_p3_2, PA_p3[6:0]}
  assign and_10_out = ~register_2_q & {PA_p3[31:9], PA_p3_2, PA_p3[6:0]};  // AND_Gate and_10, 32 bits wide

  // Notes on the sheet:
  //   contents of ROM_1 (hex, n*v repeats v):
  //   40006f 8117 ff810113 10c0006f fd010113 2812623 3010413 fca42e23 fcb42c23 fe042623 cc0006f fe042423
  //   a00006f fe842783 279793 fdc42703 f707b3 7a703 fe842783 178793 279793 fdc42683 f687b3 7a783 6e7d263
  //   fe842783 279793 fdc42703 f707b3 7a783 fef42223 fe842783 178793 279793 fdc42703 f70733 fe842783
  //   279793 fdc42683 f687b3 72703 e7a023 fe842783 178793 279793 fdc42703 f707b3 fe442703 e7a023 fe842783
  //   178793 fef42423 fd842703 fec42783 40f707b3 fff78793 fe842703 f4f748e3 fec42783 178793 fef42623
  //   fd842783 fff78793 fec42703 f2f746e3 13 13 2c12403 3010113 8067 ff010113 112623 812423 1010413 700593
  //   47b7 78513 eddff0ef 6f
  //   0 - sisend
  //   1 - valjund
endmodule

module aadressi_vordleja (
  input  [31:0] Input_bus_1,
  input  [31:0] Input_bus_2,
  output Output_1
);

  wire [31:0] xnor_1_out;

  assign xnor_1_out = ~(Input_bus_1 ^ Input_bus_2);  // XNOR_Gate xnor_1, 32 bits wide
  and and_1 (Output_1, xnor_1_out[16], xnor_1_out[2], xnor_1_out[3], xnor_1_out[4], xnor_1_out[5], xnor_1_out[6], xnor_1_out[7], xnor_1_out[8], xnor_1_out[9], xnor_1_out[10], xnor_1_out[11], xnor_1_out[12], xnor_1_out[13], xnor_1_out[14], xnor_1_out[15], xnor_1_out[17], xnor_1_out[18], xnor_1_out[19], xnor_1_out[20], xnor_1_out[21], xnor_1_out[22], xnor_1_out[23], xnor_1_out[24], xnor_1_out[25], xnor_1_out[26], xnor_1_out[27], xnor_1_out[28], xnor_1_out[29], xnor_1_out[30], xnor_1_out[31]);
endmodule

module taielik_liitja (
  input  A,
  input  B,
  input  C
);

  wire adder_1_cout, adder_1_out, and_1_out, and_2_out, or_1_out, xor_1_out, xor_2_out;

  xor xor_1 (xor_1_out, A, B);
  xor xor_2 (xor_2_out, xor_1_out, C);
  and and_1 (and_1_out, xor_1_out, C);
  and and_2 (and_2_out, B, A);
  Adder #(.width(1)) adder_1 (.a(B), .b(A), .out(adder_1_out), .cin(C), .cout(adder_1_cout));
  // Probe on xor_2_out
  // Probe on or_1_out
  or or_1 (or_1_out, and_1_out, and_2_out);
  // Probe on adder_1_out
  // Probe on adder_1_cout
endmodule

module Timer_adv (
  input  [31:0] Andmed_sisse,
  input  [31:0] Malu_aadress,
  input  [31:0] TMR_ADDR,
  input  Luba_kirjutamine,
  input  [1:0] Viigud_sisse,
  input  CLK,
  output [31:0] Andmed_valja,
  output [3:0] Erandid,
  output [1:0] Viigud_valja,
  output [1:0] Viigu_kontroll
);

  wire aadressi_vordleja_1_output_1, aadressi_vordleja_2_output_1, aadressi_vordleja_3_output_1,
       aadressi_vordleja_4_output_1, and_1_out, and_3_out, and_4_out, and_5_out, and_6_out, and_7_out,
       and_8_out, counter_1_carry, counter_2_carry, enkooder_1_kell_valja, enkooder_1_suund,
       multiplexer_2_out, multiplexer_3_out, multiplexer_4_out, multiplexer_5_out, not_2_out,
       OCR0_kokkulangevus, OCR1_kokkulangevus, or_2_out, or_3_out, or_4_out, or_5_out, undriven;
  wire [1:0] CR_q_2;
  wire [2:0] counter_1_q;
  wire [31:0] adder_1_out, adder_2_out, adder_3_out, and_2_out, counter_2_q, CR_q, multiplexer_1_out,
       or_1_out;
  wire [31:31] not_1_out;

  Adder #(.width(32)) adder_1 (.a(TMR_ADDR), .b(32'h4), .out(adder_1_out));  // open: cin, cout
  Adder #(.width(32)) adder_2 (.a(TMR_ADDR), .b(32'h8), .out(adder_2_out));  // open: cin, cout
  Adder #(.width(32)) adder_3 (.a(TMR_ADDR), .b(32'hc), .out(adder_3_out));  // open: cin, cout
  aadressi_vordleja aadressi_vordleja_1 (
    .Input_bus_1(TMR_ADDR), .Input_bus_2(Malu_aadress), .Output_1(aadressi_vordleja_1_output_1));
  aadressi_vordleja aadressi_vordleja_2 (
    .Input_bus_1(adder_1_out), .Input_bus_2(Malu_aadress), .Output_1(aadressi_vordleja_2_output_1));
  aadressi_vordleja aadressi_vordleja_3 (
    .Input_bus_1(adder_2_out), .Input_bus_2(Malu_aadress), .Output_1(aadressi_vordleja_3_output_1));
  aadressi_vordleja aadressi_vordleja_4 (
    .Input_bus_1(adder_3_out), .Input_bus_2(Malu_aadress), .Output_1(aadressi_vordleja_4_output_1));
  and and_1 (and_1_out, aadressi_vordleja_1_output_1, Luba_kirjutamine);
  enkooder enkooder_1 (
    .A(Viigud_sisse[0]), .B(Viigud_sisse[1]), .Kell_sisse(CLK), .Suund(enkooder_1_suund),
    .Kell_valja(enkooder_1_kell_valja));
  assign or_1_out = {32{1'b0}} | {CR_q[31:15], Viigu_kontroll, CR_q[12:3], CR_q_2, CR_q[0]};  // OR_Gate or_1, 32 bits wide
  assign and_2_out = {not_1_out[31], {31{1'b1}}} & or_1_out;  // AND_Gate and_2, 32 bits wide
  Multiplexer #(.width(32)) multiplexer_1 (
    .in0(Andmed_sisse), .in1(and_2_out), .out(multiplexer_1_out), .sel(or_5_out));
  Register #(.width(32)) CR (
    .D(multiplexer_1_out), .en(and_1_out), .clk(CLK),
    .Q({CR_q[31:15], Viigu_kontroll, CR_q[12:3], CR_q_2, CR_q[0]}), .clr(undriven));
  not not_1 (not_1_out[31], or_5_out);
  assign Andmed_valja = aadressi_vordleja_1_output_1 ? {CR_q[31:15], Viigu_kontroll, CR_q[12:3], CR_q_2, CR_q[0]} : 32'bz;  // Controlled_Buffer controlled_buffer_1
  Multiplexer #(.select(2)) multiplexer_2 (
    .in0(CLK), .in1(enkooder_1_kell_valja), .in2(Viigud_sisse[0]), .in3(Viigud_sisse[1]),
    .out(multiplexer_2_out), .sel(CR_q[4:3]));
  Counter #(.max('h7), .width(3)) counter_1 (
    .clr(or_3_out), .load(1'b0), .up(1'b1), .clk(multiplexer_2_out), .carry(counter_1_carry), .Q(counter_1_q));  // open: count, D
  // Probe on {CR_q[31:15], Viigu_kontroll, CR_q[12:3], CR_q_2, CR_q[0]}
  and and_3 (and_3_out, Luba_kirjutamine, aadressi_vordleja_2_output_1);
  OCR OCR0 (
    .taimeri_vaartus(counter_2_q), .andmesiin_sisse(Andmed_sisse), .WE(Luba_kirjutamine),
    .RS(aadressi_vordleja_3_output_1), .CLK(CLK), .andmesiin_valja(Andmed_valja),
    .kokkulangevus(OCR0_kokkulangevus));
  OCR OCR1 (
    .taimeri_vaartus(counter_2_q), .andmesiin_sisse(Andmed_sisse), .WE(Luba_kirjutamine),
    .RS(aadressi_vordleja_4_output_1), .CLK(CLK), .andmesiin_valja(Andmed_valja),
    .kokkulangevus(OCR1_kokkulangevus));
  or or_2 (or_2_out, counter_1_carry, or_3_out);
  or or_3 (or_3_out, ~CR_q[0], multiplexer_3_out);  // OR_Gate
  Multiplexer #(.enable("true"), .select(2)) multiplexer_3 (
    .in0(counter_1_q[0]), .in1(counter_1_q[1]), .in2(counter_1_q[2]), .in3(1'b0), .out(multiplexer_3_out),
    .sel(CR_q_2), .en(CR_q[0]));
  not not_2 (not_2_out, CR_q[5]);
  Multiplexer multiplexer_4 (.in0(not_2_out), .in1(enkooder_1_suund), .out(multiplexer_4_out), .sel(CR_q[12]));
  Multiplexer multiplexer_5 (.in0(or_2_out), .in1(CLK), .out(multiplexer_5_out), .sel(and_3_out));
  and and_4 (and_4_out, CR_q[6], OCR0_kokkulangevus);
  or or_4 (or_4_out, and_4_out, and_5_out);
  and and_5 (and_5_out, CR_q[7], OCR1_kokkulangevus);
  assign Andmed_valja = aadressi_vordleja_2_output_1 ? counter_2_q : 32'bz;  // Controlled_Buffer controlled_buffer_2
  Counter #(.max('hffffffff), .width(32)) counter_2 (
    .load(and_3_out), .D(Andmed_sisse), .count(CR_q[0]), .Q(counter_2_q), .carry(counter_2_carry),
    .up(multiplexer_4_out), .clk(multiplexer_5_out), .clr(or_4_out));
  or or_5 (or_5_out, and_8_out, and_7_out, and_6_out);
  and and_6 (and_6_out, CR_q[10], counter_2_carry);
  and and_7 (and_7_out, CR_q[8], OCR0_kokkulangevus);
  and and_8 (and_8_out, CR_q[9], OCR1_kokkulangevus);
  and and_9 (Erandid[0], counter_2_carry, CR_q[31]);
  and and_10 (Erandid[1], OCR0_kokkulangevus, CR_q[29]);
  and and_11 (Erandid[2], OCR1_kokkulangevus, CR_q[30]);
  S_R_Flip_Flop #(.trigger("low")) s_r_ff_1 (
    .S(OCR0_kokkulangevus), .R(or_4_out), .clk(1'b0), .Q(Viigud_valja[0]));  // open: reset, Qn, preset
  S_R_Flip_Flop #(.trigger("low")) s_r_ff_2 (
    .S(OCR1_kokkulangevus), .R(or_4_out), .clk(1'b0), .Q(Viigud_valja[1]));  // open: reset, Qn, preset

  // Notes on the sheet:
  //   CR - Kontrollregister
  //   0 - käivita
  //   5 - üles_alla
  //   [8 - 10] - üksik
  //   [1,2] - kella jagaja
  //   [3,4] - kella sisend
  //   [6,7] - OCR_lähtestus
  //   12 - enkoodri suuna valik
  //   [13-14] - väljundviigu kontroll
  //   29 - OCR0_võrdluskatkestus
  //   30 - OCR1_võrdluskatkestus
  //   31 - ülevoolukatkestus
endmodule

module OCR (
  input  [31:0] taimeri_vaartus,
  input  [31:0] andmesiin_sisse,
  input  WE,
  input  RS,
  input  CLK,
  output kokkulangevus,
  output [31:0] andmesiin_valja
);

  wire and_1_out;
  wire [31:0] register_1_q;

  and and_1 (and_1_out, WE, RS);
  Register #(.width(32)) register_1 (.D(andmesiin_sisse), .en(and_1_out), .clk(CLK), .Q(register_1_q));  // open: clr
  assign andmesiin_valja = RS ? register_1_q : 32'bz;  // Controlled_Buffer controlled_buffer_1
  Comparator #(.mode("unsigned"), .width(32)) comparator_1 (
    .a(taimeri_vaartus), .b(register_1_q), .eq(kokkulangevus));  // open: gt, lt
endmodule

module enkooder (
  input  A,
  input  B,
  input  Kell_sisse,
  output Suund,
  output Kell_valja
);

  wire and_1_out, and_2_out, and_3_out, and_4_out, and_5_out, and_6_out, and_7_out, and_8_out, d_ff_1_q,
       d_ff_2_q, Eelmine_A_q, Eelmine_B_q, or_2_out, or_3_out;

  D_Flip_Flop d_ff_1 (.D(A), .clk(Kell_sisse), .Q(d_ff_1_q));  // open: Qn, preset, reset
  D_Flip_Flop d_ff_2 (.D(B), .clk(Kell_sisse), .Q(d_ff_2_q));  // open: Qn, preset, reset
  D_Flip_Flop Eelmine_A (.D(d_ff_1_q), .clk(Kell_sisse), .Q(Eelmine_A_q));  // open: Qn, preset, reset
  D_Flip_Flop Eelmine_B (.D(d_ff_2_q), .clk(Kell_sisse), .Q(Eelmine_B_q));  // open: Qn, preset, reset
  and and_1 (and_1_out, d_ff_1_q, ~d_ff_2_q, ~Eelmine_A_q, ~Eelmine_B_q);  // AND_Gate
  and and_2 (and_2_out, d_ff_1_q, d_ff_2_q, Eelmine_A_q, ~Eelmine_B_q);  // AND_Gate
  and and_3 (and_3_out, ~d_ff_1_q, d_ff_2_q, Eelmine_A_q, Eelmine_B_q);  // AND_Gate
  and and_4 (and_4_out, ~d_ff_1_q, ~d_ff_2_q, ~Eelmine_A_q, Eelmine_B_q);  // AND_Gate
  and and_5 (and_5_out, ~d_ff_1_q, d_ff_2_q, ~Eelmine_A_q, ~Eelmine_B_q);  // AND_Gate
  and and_6 (and_6_out, d_ff_1_q, d_ff_2_q, ~Eelmine_A_q, Eelmine_B_q);  // AND_Gate
  and and_7 (and_7_out, d_ff_1_q, ~d_ff_2_q, Eelmine_A_q, Eelmine_B_q);  // AND_Gate
  and and_8 (and_8_out, ~d_ff_1_q, ~d_ff_2_q, Eelmine_A_q, ~Eelmine_B_q);  // AND_Gate
  or or_1 (Suund, and_1_out, and_2_out, and_3_out, and_4_out);
  or or_2 (or_2_out, and_5_out, and_6_out, and_7_out, and_8_out);
  or or_3 (or_3_out, Suund, or_2_out);
  and and_9 (Kell_valja, or_3_out, ~Kell_sisse);  // AND_Gate
endmodule
module Korrutaja (
  input  a_signed,
  input  [31:0] a,
  input  b_signed,
  input  [31:0] b,
  output [31:0] result,
  output [31:0] carry
);

  wire adder_3_cout, adder_4_cout, adder_5_cout, adder_6_cout, adder_7_cout, adder_8_cout, adder_9_cout,
       adder_10_cout, adder_11_cout, adder_12_cout, adder_13_cout, adder_14_cout, adder_15_cout,
       adder_16_cout, adder_17_cout, adder_18_cout, adder_19_cout, adder_20_cout, adder_21_cout,
       adder_22_cout, adder_23_cout, adder_24_cout, adder_25_cout, adder_26_cout, adder_27_cout,
       adder_28_cout, adder_29_cout, adder_30_cout, adder_31_cout, adder_32_cout, and_1_out, and_2_out,
       and_3_out, and_4_out, xor_1_out;
  wire [63:0] adder_1_out, adder_2_out, adder_3_out, adder_4_out, adder_5_out, adder_6_out, adder_7_out,
       adder_8_out, adder_9_out, adder_10_out, adder_11_out, adder_12_out, adder_13_out, adder_14_out,
       adder_15_out, adder_16_out, adder_17_out, adder_18_out, adder_19_out, adder_20_out, adder_21_out,
       adder_22_out, adder_23_out, adder_24_out, adder_25_out, adder_26_out, adder_27_out, adder_28_out,
       adder_29_out, adder_30_out, adder_31_out, adder_32_out, adder_33_out, adder_34_out, and_5_out,
       and_6_out, and_7_out, and_8_out, and_9_out, and_10_out, and_11_out, and_12_out, and_13_out,
       and_14_out, and_15_out, and_16_out, and_17_out, and_18_out, and_19_out, and_20_out, and_21_out,
       and_22_out, and_23_out, and_24_out, and_25_out, and_26_out, and_27_out, and_28_out, and_29_out,
       and_30_out, and_31_out, and_32_out, and_33_out, and_34_out, and_35_out, and_36_out,
       bit_extender_1_out, bit_extender_2_out, bit_extender_3_out, bit_extender_4_out, bit_extender_5_out,
       bit_extender_6_out, bit_extender_7_out, bit_extender_8_out, bit_extender_9_out, bit_extender_10_out,
       bit_extender_11_out, bit_extender_12_out, bit_extender_13_out, bit_extender_14_out,
       bit_extender_15_out, bit_extender_16_out, bit_extender_17_out, bit_extender_18_out,
       bit_extender_19_out, bit_extender_20_out, bit_extender_21_out, bit_extender_22_out,
       bit_extender_23_out, bit_extender_24_out, bit_extender_25_out, bit_extender_26_out,
       bit_extender_27_out, bit_extender_28_out, bit_extender_29_out, bit_extender_30_out,
       bit_extender_31_out, bit_extender_32_out, bit_extender_33_out, bit_extender_34_out, multiplexer_1_out,
       multiplexer_2_out, not_1_out, not_2_out, not_3_out, shifter_1_out, shifter_2_out, shifter_3_out,
       shifter_4_out, shifter_5_out, shifter_6_out, shifter_7_out, shifter_8_out, shifter_9_out,
       shifter_10_out, shifter_11_out, shifter_12_out, shifter_13_out, shifter_14_out, shifter_15_out,
       shifter_16_out, shifter_17_out, shifter_18_out, shifter_19_out, shifter_20_out, shifter_21_out,
       shifter_22_out, shifter_23_out, shifter_24_out, shifter_25_out, shifter_26_out, shifter_27_out,
       shifter_28_out, shifter_29_out, shifter_30_out, shifter_31_out;

  and and_1 (and_1_out, a_signed, a[31]);
  and and_2 (and_2_out, b_signed, b[31]);
  // Probe on b
  assign bit_extender_1_out = {{32{and_1_out}}, a};  // Bit_Extender bit_extender_1
  assign bit_extender_2_out = {{32{and_2_out}}, b};  // Bit_Extender bit_extender_2
  assign not_1_out = ~bit_extender_1_out;  // NOT_Gate not_1, 64 bits wide
  assign not_2_out = ~bit_extender_2_out;  // NOT_Gate not_2, 64 bits wide
  Adder #(.width(64)) adder_1 (.a(not_1_out), .b(64'h1), .out(adder_1_out));  // open: cin, cout
  Adder #(.width(64)) adder_2 (.a(not_2_out), .b(64'h1), .out(adder_2_out));  // open: cin, cout
  and and_3 (and_3_out, a_signed, bit_extender_1_out[63]);
  Multiplexer #(.width(64)) multiplexer_1 (
    .in0(bit_extender_1_out), .in1(adder_1_out), .out(multiplexer_1_out), .sel(and_3_out));
  and and_4 (and_4_out, b_signed, bit_extender_2_out[63]);
  Multiplexer #(.width(64)) multiplexer_2 (
    .in0(bit_extender_2_out), .in1(adder_2_out), .out(multiplexer_2_out), .sel(and_4_out));
  xor xor_1 (xor_1_out, and_3_out, and_4_out);
  Shifter #(.width(64)) shifter_1 (.in(multiplexer_1_out), .\dist (6'b000001), .out(shifter_1_out));
  Shifter #(.width(64)) shifter_2 (.in(multiplexer_1_out), .\dist (6'b000010), .out(shifter_2_out));
  Shifter #(.width(64)) shifter_3 (.in(multiplexer_1_out), .\dist (6'b000011), .out(shifter_3_out));
  Shifter #(.width(64)) shifter_4 (.in(multiplexer_1_out), .\dist (6'b000100), .out(shifter_4_out));
  Shifter #(.width(64)) shifter_5 (.in(multiplexer_1_out), .\dist (6'b000101), .out(shifter_5_out));
  Shifter #(.width(64)) shifter_6 (.in(multiplexer_1_out), .\dist (6'b000110), .out(shifter_6_out));
  Shifter #(.width(64)) shifter_7 (.in(multiplexer_1_out), .\dist (6'b000111), .out(shifter_7_out));
  Shifter #(.width(64)) shifter_8 (.in(multiplexer_1_out), .\dist (6'b001000), .out(shifter_8_out));
  Shifter #(.width(64)) shifter_9 (.in(multiplexer_1_out), .\dist (6'b001001), .out(shifter_9_out));
  Shifter #(.width(64)) shifter_10 (.in(multiplexer_1_out), .\dist (6'b001010), .out(shifter_10_out));
  Shifter #(.width(64)) shifter_11 (.in(multiplexer_1_out), .\dist (6'b001011), .out(shifter_11_out));
  Shifter #(.width(64)) shifter_12 (.in(multiplexer_1_out), .\dist (6'b001100), .out(shifter_12_out));
  Shifter #(.width(64)) shifter_13 (.in(multiplexer_1_out), .\dist (6'b001101), .out(shifter_13_out));
  Shifter #(.width(64)) shifter_14 (.in(multiplexer_1_out), .\dist (6'b001110), .out(shifter_14_out));
  Shifter #(.width(64)) shifter_15 (.in(multiplexer_1_out), .\dist (6'b001111), .out(shifter_15_out));
  Shifter #(.width(64)) shifter_16 (.in(multiplexer_1_out), .\dist (6'b010000), .out(shifter_16_out));
  Shifter #(.width(64)) shifter_17 (.in(multiplexer_1_out), .\dist (6'b010001), .out(shifter_17_out));
  Shifter #(.width(64)) shifter_18 (.in(multiplexer_1_out), .\dist (6'b010010), .out(shifter_18_out));
  Shifter #(.width(64)) shifter_19 (.in(multiplexer_1_out), .\dist (6'b010011), .out(shifter_19_out));
  Shifter #(.width(64)) shifter_20 (.in(multiplexer_1_out), .\dist (6'b010100), .out(shifter_20_out));
  Shifter #(.width(64)) shifter_21 (.in(multiplexer_1_out), .\dist (6'b010101), .out(shifter_21_out));
  Shifter #(.width(64)) shifter_22 (.in(multiplexer_1_out), .\dist (6'b010110), .out(shifter_22_out));
  Shifter #(.width(64)) shifter_23 (.in(multiplexer_1_out), .\dist (6'b010111), .out(shifter_23_out));
  Shifter #(.width(64)) shifter_24 (.in(multiplexer_1_out), .\dist (6'b011000), .out(shifter_24_out));
  Shifter #(.width(64)) shifter_25 (.in(multiplexer_1_out), .\dist (6'b011001), .out(shifter_25_out));
  Shifter #(.width(64)) shifter_26 (.in(multiplexer_1_out), .\dist (6'b011010), .out(shifter_26_out));
  Shifter #(.width(64)) shifter_27 (.in(multiplexer_1_out), .\dist (6'b011011), .out(shifter_27_out));
  Shifter #(.width(64)) shifter_28 (.in(multiplexer_1_out), .\dist (6'b011100), .out(shifter_28_out));
  Shifter #(.width(64)) shifter_29 (.in(multiplexer_1_out), .\dist (6'b011101), .out(shifter_29_out));
  Shifter #(.width(64)) shifter_30 (.in(multiplexer_1_out), .\dist (6'b011110), .out(shifter_30_out));
  Shifter #(.width(64)) shifter_31 (.in(multiplexer_1_out), .\dist (6'b011111), .out(shifter_31_out));
  assign bit_extender_3_out = {{63{multiplexer_2_out[0]}}, multiplexer_2_out[0]};  // Bit_Extender bit_extender_3
  assign bit_extender_4_out = {{63{multiplexer_2_out[1]}}, multiplexer_2_out[1]};  // Bit_Extender bit_extender_4
  assign bit_extender_5_out = {{63{multiplexer_2_out[2]}}, multiplexer_2_out[2]};  // Bit_Extender bit_extender_5
  assign bit_extender_6_out = {{63{multiplexer_2_out[3]}}, multiplexer_2_out[3]};  // Bit_Extender bit_extender_6
  assign bit_extender_7_out = {{63{multiplexer_2_out[4]}}, multiplexer_2_out[4]};  // Bit_Extender bit_extender_7
  assign bit_extender_8_out = {{63{multiplexer_2_out[5]}}, multiplexer_2_out[5]};  // Bit_Extender bit_extender_8
  assign bit_extender_9_out = {{63{multiplexer_2_out[6]}}, multiplexer_2_out[6]};  // Bit_Extender bit_extender_9
  assign bit_extender_10_out = {{63{multiplexer_2_out[7]}}, multiplexer_2_out[7]};  // Bit_Extender bit_extender_10
  assign bit_extender_11_out = {{63{multiplexer_2_out[8]}}, multiplexer_2_out[8]};  // Bit_Extender bit_extender_11
  assign bit_extender_12_out = {{63{multiplexer_2_out[9]}}, multiplexer_2_out[9]};  // Bit_Extender bit_extender_12
  assign bit_extender_13_out = {{63{multiplexer_2_out[10]}}, multiplexer_2_out[10]};  // Bit_Extender bit_extender_13
  assign bit_extender_14_out = {{63{multiplexer_2_out[11]}}, multiplexer_2_out[11]};  // Bit_Extender bit_extender_14
  assign bit_extender_15_out = {{63{multiplexer_2_out[12]}}, multiplexer_2_out[12]};  // Bit_Extender bit_extender_15
  assign bit_extender_16_out = {{63{multiplexer_2_out[13]}}, multiplexer_2_out[13]};  // Bit_Extender bit_extender_16
  assign bit_extender_17_out = {{63{multiplexer_2_out[14]}}, multiplexer_2_out[14]};  // Bit_Extender bit_extender_17
  assign bit_extender_18_out = {{63{multiplexer_2_out[15]}}, multiplexer_2_out[15]};  // Bit_Extender bit_extender_18
  assign bit_extender_19_out = {{63{multiplexer_2_out[16]}}, multiplexer_2_out[16]};  // Bit_Extender bit_extender_19
  assign bit_extender_20_out = {{63{multiplexer_2_out[17]}}, multiplexer_2_out[17]};  // Bit_Extender bit_extender_20
  assign bit_extender_21_out = {{63{multiplexer_2_out[18]}}, multiplexer_2_out[18]};  // Bit_Extender bit_extender_21
  assign bit_extender_22_out = {{63{multiplexer_2_out[19]}}, multiplexer_2_out[19]};  // Bit_Extender bit_extender_22
  assign bit_extender_23_out = {{63{multiplexer_2_out[20]}}, multiplexer_2_out[20]};  // Bit_Extender bit_extender_23
  assign bit_extender_24_out = {{63{multiplexer_2_out[21]}}, multiplexer_2_out[21]};  // Bit_Extender bit_extender_24
  assign bit_extender_25_out = {{63{multiplexer_2_out[22]}}, multiplexer_2_out[22]};  // Bit_Extender bit_extender_25
  assign bit_extender_26_out = {{63{multiplexer_2_out[23]}}, multiplexer_2_out[23]};  // Bit_Extender bit_extender_26
  assign bit_extender_27_out = {{63{multiplexer_2_out[24]}}, multiplexer_2_out[24]};  // Bit_Extender bit_extender_27
  assign bit_extender_28_out = {{63{multiplexer_2_out[25]}}, multiplexer_2_out[25]};  // Bit_Extender bit_extender_28
  assign bit_extender_29_out = {{63{multiplexer_2_out[26]}}, multiplexer_2_out[26]};  // Bit_Extender bit_extender_29
  assign bit_extender_30_out = {{63{multiplexer_2_out[27]}}, multiplexer_2_out[27]};  // Bit_Extender bit_extender_30
  assign bit_extender_31_out = {{63{multiplexer_2_out[28]}}, multiplexer_2_out[28]};  // Bit_Extender bit_extender_31
  assign bit_extender_32_out = {{63{multiplexer_2_out[29]}}, multiplexer_2_out[29]};  // Bit_Extender bit_extender_32
  assign bit_extender_33_out = {{63{multiplexer_2_out[30]}}, multiplexer_2_out[30]};  // Bit_Extender bit_extender_33
  assign bit_extender_34_out = {{63{multiplexer_2_out[31]}}, multiplexer_2_out[31]};  // Bit_Extender bit_extender_34
  assign and_5_out = bit_extender_3_out & multiplexer_1_out;  // AND_Gate and_5, 64 bits wide
  assign and_6_out = bit_extender_4_out & shifter_1_out;  // AND_Gate and_6, 64 bits wide
  assign and_7_out = bit_extender_5_out & shifter_2_out;  // AND_Gate and_7, 64 bits wide
  assign and_8_out = bit_extender_6_out & shifter_3_out;  // AND_Gate and_8, 64 bits wide
  assign and_9_out = bit_extender_7_out & shifter_4_out;  // AND_Gate and_9, 64 bits wide
  assign and_10_out = bit_extender_8_out & shifter_5_out;  // AND_Gate and_10, 64 bits wide
  assign and_11_out = bit_extender_9_out & shifter_6_out;  // AND_Gate and_11, 64 bits wide
  assign and_12_out = bit_extender_10_out & shifter_7_out;  // AND_Gate and_12, 64 bits wide
  assign and_13_out = bit_extender_11_out & shifter_8_out;  // AND_Gate and_13, 64 bits wide
  assign and_14_out = bit_extender_12_out & shifter_9_out;  // AND_Gate and_14, 64 bits wide
  assign and_15_out = bit_extender_13_out & shifter_10_out;  // AND_Gate and_15, 64 bits wide
  assign and_16_out = bit_extender_14_out & shifter_11_out;  // AND_Gate and_16, 64 bits wide
  assign and_17_out = bit_extender_15_out & shifter_12_out;  // AND_Gate and_17, 64 bits wide
  assign and_18_out = bit_extender_16_out & shifter_13_out;  // AND_Gate and_18, 64 bits wide
  assign and_19_out = bit_extender_17_out & shifter_14_out;  // AND_Gate and_19, 64 bits wide
  assign and_20_out = bit_extender_18_out & shifter_15_out;  // AND_Gate and_20, 64 bits wide
  assign and_21_out = bit_extender_19_out & shifter_16_out;  // AND_Gate and_21, 64 bits wide
  assign and_22_out = bit_extender_20_out & shifter_17_out;  // AND_Gate and_22, 64 bits wide
  assign and_23_out = bit_extender_21_out & shifter_18_out;  // AND_Gate and_23, 64 bits wide
  assign and_24_out = bit_extender_22_out & shifter_19_out;  // AND_Gate and_24, 64 bits wide
  assign and_25_out = bit_extender_23_out & shifter_20_out;  // AND_Gate and_25, 64 bits wide
  assign and_26_out = bit_extender_24_out & shifter_21_out;  // AND_Gate and_26, 64 bits wide
  assign and_27_out = bit_extender_25_out & shifter_22_out;  // AND_Gate and_27, 64 bits wide
  assign and_28_out = bit_extender_26_out & shifter_23_out;  // AND_Gate and_28, 64 bits wide
  assign and_29_out = bit_extender_27_out & shifter_24_out;  // AND_Gate and_29, 64 bits wide
  assign and_30_out = bit_extender_28_out & shifter_25_out;  // AND_Gate and_30, 64 bits wide
  assign and_31_out = bit_extender_29_out & shifter_26_out;  // AND_Gate and_31, 64 bits wide
  assign and_32_out = bit_extender_30_out & shifter_27_out;  // AND_Gate and_32, 64 bits wide
  assign and_33_out = bit_extender_31_out & shifter_28_out;  // AND_Gate and_33, 64 bits wide
  assign and_34_out = bit_extender_32_out & shifter_29_out;  // AND_Gate and_34, 64 bits wide
  assign and_35_out = bit_extender_33_out & shifter_30_out;  // AND_Gate and_35, 64 bits wide
  assign and_36_out = bit_extender_34_out & shifter_31_out;  // AND_Gate and_36, 64 bits wide
  Adder #(.width(64)) adder_3 (.a(and_5_out), .b(and_6_out), .out(adder_3_out), .cout(adder_3_cout));  // open: cin
  Adder #(.width(64)) adder_4 (
    .a(adder_3_out), .b(and_7_out), .out(adder_4_out), .cin(adder_3_cout), .cout(adder_4_cout));
  Adder #(.width(64)) adder_5 (
    .a(adder_4_out), .b(and_8_out), .out(adder_5_out), .cin(adder_4_cout), .cout(adder_5_cout));
  Adder #(.width(64)) adder_6 (
    .a(adder_5_out), .b(and_9_out), .out(adder_6_out), .cin(adder_5_cout), .cout(adder_6_cout));
  Adder #(.width(64)) adder_7 (
    .a(adder_6_out), .b(and_10_out), .out(adder_7_out), .cin(adder_6_cout), .cout(adder_7_cout));
  Adder #(.width(64)) adder_8 (
    .a(adder_7_out), .b(and_11_out), .out(adder_8_out), .cin(adder_7_cout), .cout(adder_8_cout));
  Adder #(.width(64)) adder_9 (
    .a(adder_8_out), .b(and_12_out), .out(adder_9_out), .cin(adder_8_cout), .cout(adder_9_cout));
  Adder #(.width(64)) adder_10 (
    .a(adder_9_out), .b(and_13_out), .out(adder_10_out), .cin(adder_9_cout), .cout(adder_10_cout));
  Adder #(.width(64)) adder_11 (
    .a(adder_10_out), .b(and_14_out), .out(adder_11_out), .cin(adder_10_cout), .cout(adder_11_cout));
  Adder #(.width(64)) adder_12 (
    .a(adder_11_out), .b(and_15_out), .out(adder_12_out), .cin(adder_11_cout), .cout(adder_12_cout));
  Adder #(.width(64)) adder_13 (
    .a(adder_12_out), .b(and_16_out), .out(adder_13_out), .cin(adder_12_cout), .cout(adder_13_cout));
  Adder #(.width(64)) adder_14 (
    .a(adder_13_out), .b(and_17_out), .out(adder_14_out), .cin(adder_13_cout), .cout(adder_14_cout));
  Adder #(.width(64)) adder_15 (
    .a(adder_14_out), .b(and_18_out), .out(adder_15_out), .cin(adder_14_cout), .cout(adder_15_cout));
  Adder #(.width(64)) adder_16 (
    .a(adder_15_out), .b(and_19_out), .out(adder_16_out), .cin(adder_15_cout), .cout(adder_16_cout));
  Adder #(.width(64)) adder_17 (
    .a(adder_16_out), .b(and_20_out), .out(adder_17_out), .cin(adder_16_cout), .cout(adder_17_cout));
  Adder #(.width(64)) adder_18 (
    .a(adder_17_out), .b(and_21_out), .out(adder_18_out), .cin(adder_17_cout), .cout(adder_18_cout));
  Adder #(.width(64)) adder_19 (
    .a(adder_18_out), .b(and_22_out), .out(adder_19_out), .cin(adder_18_cout), .cout(adder_19_cout));
  Adder #(.width(64)) adder_20 (
    .a(adder_19_out), .b(and_23_out), .out(adder_20_out), .cin(adder_19_cout), .cout(adder_20_cout));
  Adder #(.width(64)) adder_21 (
    .a(adder_20_out), .b(and_24_out), .out(adder_21_out), .cin(adder_20_cout), .cout(adder_21_cout));
  Adder #(.width(64)) adder_22 (
    .a(adder_21_out), .b(and_25_out), .out(adder_22_out), .cin(adder_21_cout), .cout(adder_22_cout));
  Adder #(.width(64)) adder_23 (
    .a(adder_22_out), .b(and_26_out), .out(adder_23_out), .cin(adder_22_cout), .cout(adder_23_cout));
  Adder #(.width(64)) adder_24 (
    .a(adder_23_out), .b(and_27_out), .out(adder_24_out), .cin(adder_23_cout), .cout(adder_24_cout));
  Adder #(.width(64)) adder_25 (
    .a(adder_24_out), .b(and_28_out), .out(adder_25_out), .cin(adder_24_cout), .cout(adder_25_cout));
  Adder #(.width(64)) adder_26 (
    .a(adder_25_out), .b(and_29_out), .out(adder_26_out), .cin(adder_25_cout), .cout(adder_26_cout));
  Adder #(.width(64)) adder_27 (
    .a(adder_26_out), .b(and_30_out), .out(adder_27_out), .cin(adder_26_cout), .cout(adder_27_cout));
  Adder #(.width(64)) adder_28 (
    .a(adder_27_out), .b(and_31_out), .out(adder_28_out), .cin(adder_27_cout), .cout(adder_28_cout));
  Adder #(.width(64)) adder_29 (
    .a(adder_28_out), .b(and_32_out), .out(adder_29_out), .cin(adder_28_cout), .cout(adder_29_cout));
  Adder #(.width(64)) adder_30 (
    .a(adder_29_out), .b(and_33_out), .out(adder_30_out), .cin(adder_29_cout), .cout(adder_30_cout));
  Adder #(.width(64)) adder_31 (
    .a(adder_30_out), .b(and_34_out), .out(adder_31_out), .cin(adder_30_cout), .cout(adder_31_cout));
  Adder #(.width(64)) adder_32 (
    .a(adder_31_out), .b(and_35_out), .out(adder_32_out), .cin(adder_31_cout), .cout(adder_32_cout));
  Adder #(.width(64)) adder_33 (
    .a(adder_32_out), .b(and_36_out), .out(adder_33_out), .cin(adder_32_cout));  // open: cout
  assign not_3_out = ~adder_33_out;  // NOT_Gate not_3, 64 bits wide
  Adder #(.width(64)) adder_34 (.a(not_3_out), .b(64'h1), .out(adder_34_out));  // open: cin, cout
  Multiplexer #(.width(64)) multiplexer_3 (
    .in0(adder_33_out), .in1(adder_34_out), .out({carry, result}), .sel(xor_1_out));
endmodule

module ALU_RV32I (
  input  [4:0] Juhend,
  input  [31:0] a1,
  input  [31:0] a2,
  output [31:0] Tulemus
);

  wire adder_1_cout, comparator_1_lt, decoder_1_out1, decoder_1_out2, decoder_1_out22, decoder_1_out23,
       not_1_out, or_1_out;
  wire [31:0] adder_1_out, and_1_out, bit_extender_1_out, bit_extender_2_out, bit_extender_3_out, or_2_out,
       shifter_1_out, shifter_2_out, shifter_3_out, xor_1_out, xor_2_out;

  Decoder #(.enable("false"), .select(5)) decoder_1 (
    .out1(decoder_1_out1), .out2(decoder_1_out2), .out22(decoder_1_out22), .out23(decoder_1_out23),
    .sel(Juhend));  // open: out0, out3, out4, out5, out6, out7, out8, out9, out10, out11, out12, out13, out14, out15, out16, out17, out18, out19, out20, out21, out24, out25, out26, out27, out28, out29, out30, out31
  or or_1 (or_1_out, decoder_1_out1, decoder_1_out2);
  assign bit_extender_1_out = {{31{or_1_out}}, or_1_out};  // Bit_Extender bit_extender_1
  assign xor_1_out = bit_extender_1_out ^ a2;  // XOR_Gate xor_1, 32 bits wide
  Adder #(.width(32)) adder_1 (.a(a1), .b(xor_1_out), .out(adder_1_out), .cin(or_1_out), .cout(adder_1_cout));
  not not_1 (not_1_out, adder_1_cout);
  Shifter #(.width(32)) shifter_1 (.in(a1), .\dist (a2[4:0]), .out(shifter_1_out));
  Shifter #(.shift("lr"), .width(32)) shifter_2 (.in(a1), .\dist (a2[4:0]), .out(shifter_2_out));
  Shifter #(.shift("ar"), .width(32)) shifter_3 (.in(a1), .\dist (a2[4:0]), .out(shifter_3_out));
  assign and_1_out = a1 & a2;  // AND_Gate and_1, 32 bits wide
  assign or_2_out = a1 | a2;  // OR_Gate or_2, 32 bits wide
  assign xor_2_out = a1 ^ a2;  // XOR_Gate xor_2, 32 bits wide
  Comparator #(.width(32)) comparator_1 (.a(a1), .b(a2), .lt(comparator_1_lt));  // open: gt, eq
  assign bit_extender_2_out = {{31{1'b0}}, not_1_out};  // Bit_Extender bit_extender_2
  assign bit_extender_3_out = {{31{1'b0}}, comparator_1_lt};  // Bit_Extender bit_extender_3
  Multiplexer #(.select(5), .width(32)) multiplexer_1 (
    .in0(adder_1_out), .in1(adder_1_out), .in2(bit_extender_2_out), .in3(shifter_1_out), .in4(shifter_2_out),
    .in5(shifter_3_out), .in6(and_1_out), .in7(or_2_out), .in8(xor_2_out), .in9(bit_extender_3_out),
    .out(Tulemus), .sel(Juhend));  // open: in10, in11, in12, in13, in14, in15, in16, in17, in18, in19, in20, in21, in22, in23, in24, in25, in26, in27, in28, in29, in30, in31
endmodule
